// Digital circuit DigLo69_Project-3.dig as structural Verilog
module DigLo69_Project_3 (
  input  [7:0] M,
  input  [7:0] N,
  input  [13:0] progIn,
  input  reset,
  input  progLoad,
  input  start,
  input  result,
  input  clk,
  output valid,
  output done,
  output [7:0] \output ,
  output [7:0] out_12
);

  wire _00, _0000, _0001, _01, _0010, _10, _0011, _11, _0100, _0101, _0110, _0111, _1000, _1001, _1010,
       _1011, _1100, _1101, _1110, _1111, accA_accB, accA_operand, accA_pRAMoperand, accA_regC, accA_regD,
       accA_rRAMoperand, accA_rRAMregC, accA_rRAMSP, accA_SP, accB_accA, accB_operand, and_1_out, and_2_out,
       and_3_out, and_4_out, and_5_out, and_6_out, and_7_out, and_8_out, and_9_out, and_10_out, and_11_out,
       and_12_out, and_13_out, and_14_out, and_15_out, and_16_out, and_20_out, and_22_out, and_23_out,
       and_43_out, and_44_out, and_45_out, and_46_out, and_50_out, and_51_out, and_52_out, and_53_out,
       and_65_out, and_66_out, and_67_out, and_68_out, and_69_out, and_70_out, and_71_out, and_72_out,
       and_74_out, CALL, comparator_2_eq, comparator_4_eq, comparator_5_lt, comparator_6_gt, comparator_7_eq,
       comparator_7_gt, comparator_7_lt, comparator_8_eq, comparator_9_eq, End, eq, F00, F01, F10, F11,
       FiboN__eq__eq__0, FQa, FQb, GCD_accA, GCD_accA1, GCD_accAPrime, GCD_accB, GCD_accB1, GCD_accBPrime,
       GCD_equal, gr, isFibo, isGCD, isHALT, isPrime, isPrime_2_d, isPrime_3_d, isSSUM, jump, jump_regD,
       load_accA, load_accB, load_eq, load_gr, load_ls, load_regC, load_regD, load_SP, load_valid, loadFiboA,
       loadFiboB, loadN, LoadSSP, LoadSSum, ls, multiplexer_3_out, multiplexer_5_out, multiplexer_10_out,
       multiplexer_28_out, multiplexer_29_out, multiplexer_30_out, multiplexer_31_out, multiplexer_32_out,
       multiplexer_33_out, multiplexer_34_out, multiplexer_35_out, multiplexer_36_out, multiplexer_38_out,
       multiplexer_44_out, multiplexer_47_out, multiplexer_50_out, multiplexer_51_out, multiplexer_52_out,
       multiplexer_53_out, multiplexer_54_out, nor_1_out, nor_2_out, not_1_out, not_2_out, not_3_out,
       not_4_out, not_5_out, not_6_out, not_7_out, not_8_out, not_9_out, not_10_out, not_11_out, not_12_out,
       not_13_out, not_14_out, not_16_out, notconnected_1_out, notconnected_2_out, notconnected_3_out,
       notconnected_4_out, notconnected_5_out, notconnected_6_out, notconnected_7_out, notconnected_8_out,
       notconnected_9_out, notconnected_10_out, notconnected_11_out, notconnected_12_out, or_1_out, or_2_out,
       or_5_out, or_6_out, or_7_out, or_8_out, or_10_out, or_11_out, or_12_out, or_13_out, or_14_out,
       or_15_out, or_16_out, or_17_out, or_18_out, or_19_out, or_20_out, or_21_out, or_25_out, or_26_out,
       or_28_out, or_29_out, or_30_out, or_32_out, or_36_out, or_38_out, or_40_out, or_42_out, Read_rRAM,
       redone, regC_accA, regC_M, regD_accA, regD_N, reset_lt_16, reset_state, RET, rRAM_accA,
       rRAM_iter__lt__16, rRAM_operand, rRAM_regC, rRAM_SP, S0000, S0001, S0010, S0011, S0100, S0101, S0110,
       S0111, S1000, S1001, S1010, S1011, S1100, S1101, S1110, S1111, Sa, Sb, Sc, Sd, SP_pop, SP_push, SS000,
       SS001, SS010, SS011, SS100, SS101, SS110, SS111, useALU, useSP, Write_rRAM;
  wire [0:0] Prime;
  wire [1:0] group;
  wire [2:0] SS;
  wire [3:0] ALU;
  wire [4:0] FiboN, multiplexer_17_out, sub_1_s;
  wire [7:0] A, accA, accB, accB_GCD, add_2_s, add_3_s, add_6_s, \and , B, C, D, Diff, multiplexer_1_out,
       multiplexer_4_out, multiplexer_6_out, multiplexer_7_out, multiplexer_8_out, multiplexer_9_out,
       multiplexer_11_out, multiplexer_12_out, multiplexer_13_out, multiplexer_15_out, multiplexer_16_out,
       multiplexer_18_out, multiplexer_23_out, multiplexer_24_out, multiplexer_25_out, multiplexer_26_out,
       multiplexer_37_out, multiplexer_39_out, multiplexer_40_out, multiplexer_41_out, multiplexer_42_out,
       multiplexer_43_out, multiplexer_45_out, multiplexer_46_out, multiplexer_48_out, multiplexer_49_out,
       multiplexer_55_out, multiplexer_56_out, multiplexer_57_out, multiplexer_58_out, multiplexer_59_out,
       multiplexer_60_out, multiplexer_61_out, multiplexer_62_out, multiplexer_63_out, multiplexer_64_out,
       multiplexer_65_out, multiplexer_66_out, multiplexer_67_out, multiplexer_68_out, multiplexer_70_out,
       multiplexer_71_out, multiplexer_72_out, multiplexer_75_out, multiplexer_76_out, Multy, na, operand,
       \or , PC, PC_rRAM, pRAM_Counter, quotient, regC, regD, remain, reset_iter, rotateShiftLeft,
       rotateShiftRight, rRAM, rRAM_address, rRAM_d, rRAM_Din, rRAM_Iter, shiftLeft, shiftRight, SP, SSP,
       sub_2_s, sub_5_s, Sum, \xor ;
  wire [13:8] pRAM_d;
  wire [15:0] add_1_s, add_4_s, FiboA, FiboB, multiplexer_2_out, multiplexer_21_out, multiplexer_22_out, SSum;

  Add #(.Bits(16)) add_1 (.a(SSum), .b({{8{1'b0}}, rRAM}), .c_i(1'b0), .s(add_1_s));  // open: c_o
  Add #(.Bits(8)) add_2 (.a(SSP), .b(8'h1), .c_i(1'b0), .s(add_2_s));  // open: c_o
  Multiplexer #(.Bits(8)) multiplexer_1 (.sel(not_1_out), .in_0(SP), .in_1(add_2_s), .out(multiplexer_1_out));
  Multiplexer #(.Bits(16)) multiplexer_2 (.sel(not_2_out), .in_0({16{1'b0}}), .in_1(add_1_s), .out(multiplexer_2_out));
  not not_1 (not_1_out, SS000);
  not not_2 (not_2_out, SS000);
  Multiplexer #(.Selector_Bits(3)) multiplexer_3 (
    .sel(SS), .in_0(1'b0), .in_1(End), .in_2(1'b0), .in_3(1'b0), .in_4(1'b1), .in_5(1'b0), .in_6(1'b0),
    .in_7(1'b0), .out(multiplexer_3_out));
  D_FF d_ff_1 (.D(multiplexer_3_out), .C(clk), .Q(SS[2]));  // open: nQ
  Register #(.Bits(8)) register_1 (.D(multiplexer_1_out), .C(clk), .en(LoadSSP), .Q(SSP));
  Register #(.Bits(16)) register_2 (.D(multiplexer_2_out), .C(clk), .en(LoadSSum), .Q(SSum));
  Comparator #(.Bits(8)) comparator_1 (.a(SSP), .b({8{1'b0}}), .eq(End));  // open: gt, lt
  Add #(.Bits(8)) add_3 (.a(PC), .b(8'h1), .c_i(1'b0), .s(add_3_s));  // open: c_o
  and and_1 (and_1_out, _1000, S0101);
  not not_3 (not_3_out, End);
  Multiplexer #(.Bits(8)) multiplexer_4 (.sel(SS101), .in_0({8{1'b0}}), .in_1(SSum[7:0]), .out(multiplexer_4_out));
  and and_2 (and_2_out, S0101, _01, _1100);
  or or_1 (or_1_out, _0001, _0101, and_1_out);
  Multiplexer #(.Selector_Bits(3)) multiplexer_5 (
    .sel(SS), .in_0(1'b0), .in_1(not_3_out), .in_2(1'b1), .in_3(1'b0), .in_4(1'b0), .in_5(1'b0), .in_6(1'b0),
    .in_7(1'b0), .out(multiplexer_5_out));
  Multiplexer #(.Bits(8)) multiplexer_6 (
    .sel(SS100), .in_0(multiplexer_4_out), .in_1(SSum[15:8]), .out(multiplexer_6_out));
  D_FF d_ff_2 (.D(multiplexer_5_out), .C(clk), .Q(SS[1]));  // open: nQ
  Multiplexer #(.Bits(8)) multiplexer_7 (
    .sel(and_2_out), .in_0(multiplexer_6_out), .in_1(add_3_s), .out(multiplexer_7_out));
  and and_3 (and_3_out, _01, or_1_out);
  or or_2 (or_2_out, _1000, _1100);
  Multiplexer #(.Bits(8)) multiplexer_8 (
    .sel(and_3_out), .in_0(multiplexer_7_out), .in_1(accA), .out(multiplexer_8_out));
  or or_3 (LoadSSum, SS010, SS000);
  or or_4 (LoadSSP, SS011, SS000);
  Multiplexer #(.Bits(8)) multiplexer_9 (.sel(S0110), .in_0(rRAM_address), .in_1(rRAM_Iter), .out(multiplexer_9_out));
  Multiplexer #(.Selector_Bits(3)) multiplexer_10 (
    .sel(SS), .in_0(S1101), .in_1(1'b0), .in_2(1'b1), .in_3(1'b1), .in_4(1'b1), .in_5(1'b0), .in_6(1'b0),
    .in_7(1'b0), .out(multiplexer_10_out));
  Decoder #(.Selector_Bits(3)) decoder_1 (
    .sel(SS), .out_0(SS000), .out_1(SS001), .out_2(SS010), .out_3(SS011), .out_4(SS100), .out_5(SS101),
    .out_6(SS110), .out_7(SS111));
  and and_4 (and_4_out, or_2_out, S0101);
  Multiplexer #(.Bits(8)) multiplexer_11 (
    .sel(F10), .in_0(multiplexer_8_out), .in_1(FiboA[15:8]), .out(multiplexer_11_out));
  Multiplexer #(.Bits(8)) multiplexer_12 (
    .sel(reset_state), .in_0(multiplexer_9_out), .in_1(reset_iter), .out(multiplexer_12_out));
  D_FF d_ff_3 (.D(multiplexer_10_out), .C(clk), .Q(SS[0]));  // open: nQ
  or or_5 (or_5_out, _0001, _0101, and_4_out);
  or or_6 (or_6_out, F10, F11);
  or or_7 (or_7_out, SS101, SS100);
  or or_8 (or_8_out, _1100, _1101);
  Comparator #(.Bits(8)) comparator_2 (.a(regD), .b({8{1'b0}}), .eq(comparator_2_eq));  // open: gt, lt
  Multiplexer #(.Bits(8)) multiplexer_13 (
    .sel(F11), .in_0(multiplexer_11_out), .in_1(FiboA[7:0]), .out(multiplexer_13_out));
  Multiplexer #(.Bits(8)) multiplexer_14 (.sel(reset), .in_0(multiplexer_13_out), .in_1({8{1'b0}}), .out(rRAM_Din));
  and and_5 (and_5_out, _11, _0010, gr);
  and and_6 (and_6_out, _11, _0000);
  and and_7 (and_7_out, _11, _0001, eq);
  and and_8 (and_8_out, _11, _0011, ls);
  and and_9 (and_9_out, _01, or_8_out);
  and and_10 (and_10_out, _11, _0100, ~comparator_2_eq);  // And
  and and_11 (and_11_out, _01, or_5_out);
  and and_12 (and_12_out, _11, or_6_out, _1101);
  and and_13 (and_13_out, _11, _1110, or_7_out);
  RAMDualPort #(.AddrBits(8), .Bits(8)) u_rRAM (
    .A(multiplexer_12_out), .Din(rRAM_Din), .str(Write_rRAM), .C(clk), .ld(1'b1), .D(rRAM_d));
  Sub #(.Bits(5)) sub_1 (.a(FiboN), .b(5'b00001), .c_i(1'b0), .s(sub_1_s));  // open: c_o
  or or_9 (Write_rRAM, reset, and_11_out, and_12_out, and_13_out);
  and and_14 (and_14_out, _01, _1101, S0100);
  Add #(.Bits(16)) add_4 (.a(FiboA), .b(FiboB), .c_i(1'b0), .s(add_4_s));  // open: c_o
  Multiplexer #(.Bits(8)) multiplexer_15 (.sel(SS101), .in_0({8{1'b0}}), .in_1(8'hd), .out(multiplexer_15_out));
  Multiplexer #(.Bits(8)) multiplexer_16 (
    .sel(SS100), .in_0(multiplexer_15_out), .in_1(8'hc), .out(multiplexer_16_out));
  and and_15 (and_15_out, S1101, ~SS100, ~SS101);  // And
  Multiplexer #(.Bits(5)) multiplexer_17 (.sel(F00), .in_0(sub_1_s), .in_1(accA[4:0]), .out(multiplexer_17_out));
  or or_10 (or_10_out, and_5_out, and_6_out, and_7_out, and_8_out, and_9_out, and_10_out);
  Multiplexer #(.Bits(8)) multiplexer_18 (
    .sel(and_15_out), .in_0(multiplexer_16_out), .in_1(SSP), .out(multiplexer_18_out));
  Multiplexer #(.Bits(8)) multiplexer_19 (.sel(Read_rRAM), .in_0({8{1'b0}}), .in_1(rRAM_d), .out(rRAM));
  Multiplexer #(.Bits(8)) multiplexer_20 (.sel(and_16_out), .in_0({8{1'b0}}), .in_1(rRAM_d), .out(\output ));
  and and_16 (and_16_out, rRAM_iter__lt__16, S0110);
  Register #(.Bits(8)) register_3 (.D(rRAM), .C(clk), .en(and_14_out), .Q(PC_rRAM));
  Multiplexer #(.Bits(16)) multiplexer_21 (.sel(F00), .in_0(FiboB), .in_1({16{1'b0}}), .out(multiplexer_21_out));
  Multiplexer #(.Bits(16)) multiplexer_22 (.sel(F00), .in_0(add_4_s), .in_1(16'h1), .out(multiplexer_22_out));
  and and_17 (jump, or_10_out, S0011);
  or or_11 (or_11_out, _0100, _0101);
  Multiplexer #(.Bits(8)) multiplexer_23 (.sel(F10), .in_0(multiplexer_18_out), .in_1(8'ha), .out(multiplexer_23_out));
  or or_12 (or_12_out, _0000, _0001, _0010);
  Multiplexer #(.Bits(8)) multiplexer_24 (.sel(F11), .in_0(multiplexer_23_out), .in_1(8'hb), .out(multiplexer_24_out));
  Register #(.Bits(16)) u_FiboA (.D(multiplexer_21_out), .C(clk), .en(loadFiboA), .Q(FiboA));
  Register #(.Bits(16)) u_FiboB (.D(multiplexer_22_out), .C(clk), .en(loadFiboB), .Q(FiboB));
  and and_18 (rRAM_operand, _01, or_12_out);
  and and_19 (rRAM_regC, _01, or_11_out);
  Multiplexer #(.Bits(8)) multiplexer_25 (
    .sel(rRAM_SP), .in_0(multiplexer_24_out), .in_1(SP), .out(multiplexer_25_out));
  Register #(.Bits(5)) u_FiboN (.D(multiplexer_17_out), .C(clk), .en(loadN), .Q(FiboN));
  Comparator #(.Bits(5)) comparator_3 (.a(multiplexer_17_out), .b({5{1'b0}}), .eq(FiboN__eq__eq__0));  // open: gt, lt
  Multiplexer #(.Bits(8)) multiplexer_26 (
    .sel(rRAM_regC), .in_0(multiplexer_25_out), .in_1(regC), .out(multiplexer_26_out));
  Comparator #(.Signed("true"), .Bits(8)) comparator_4 (.a(accA), .b(accB), .eq(comparator_4_eq));  // open: gt, lt
  ROM #(.AddrBits(8)) u_isPrime (.A(accA), .sel(1'b1), .D(Prime[0]));
  Multiplexer #(.Bits(8)) multiplexer_27 (
    .sel(rRAM_operand), .in_0(multiplexer_26_out), .in_1(operand), .out(rRAM_address));
  Comparator #(.Signed("true"), .Bits(8)) comparator_5 (.a(accA), .b(accB), .lt(comparator_5_lt));  // open: gt, eq
  Comparator #(.Signed("true"), .Bits(8)) comparator_6 (.a(accA), .b(accB), .gt(comparator_6_gt));  // open: eq, lt
  Multiplexer multiplexer_28 (.sel(isPrime), .in_0(comparator_4_eq), .in_1(Prime[0]), .out(multiplexer_28_out));
  Multiplexer multiplexer_29 (.sel(reset), .in_0(comparator_6_gt), .in_1(1'b0), .out(multiplexer_29_out));
  Multiplexer multiplexer_30 (.sel(reset), .in_0(multiplexer_28_out), .in_1(1'b0), .out(multiplexer_30_out));
  Multiplexer multiplexer_31 (.sel(reset), .in_0(comparator_5_lt), .in_1(1'b0), .out(multiplexer_31_out));
  not not_4 (not_4_out, rRAM_iter__lt__16);
  Register u_gr (.D(multiplexer_29_out), .C(clk), .en(load_gr), .Q(gr));
  Register u_eq (.D(multiplexer_30_out), .C(clk), .en(load_eq), .Q(eq));
  Register u_ls (.D(multiplexer_31_out), .C(clk), .en(load_ls), .Q(ls));
  not not_5 (not_5_out, rRAM_iter__lt__16);
  Multiplexer multiplexer_32 (.sel(start), .in_0(not_4_out), .in_1(1'b0), .out(multiplexer_32_out));
  not not_6 (not_6_out, rRAM_iter__lt__16);
  and and_20 (and_20_out, FiboN__eq__eq__0, S1100);
  or or_13 (or_13_out, not_5_out, redone);
  Multiplexer multiplexer_33 (.sel(result), .in_0(multiplexer_32_out), .in_1(1'b0), .out(multiplexer_33_out));
  or or_14 (or_14_out, not_6_out, result, start, progLoad);
  and and_21 (done, or_13_out, ~start);  // And
  Register register_4 (.D(multiplexer_33_out), .C(clk), .en(or_14_out), .Q(redone));
  Multiplexer #(.Selector_Bits(2)) multiplexer_34 (
    .sel({FQa, FQb}), .in_0(and_20_out), .in_1(FiboN__eq__eq__0), .in_2(1'b1), .in_3(1'b0),
    .out(multiplexer_34_out));
  D_FF d_ff_4 (.D(multiplexer_34_out), .C(clk), .Q(FQa));  // open: nQ
  or or_15 (or_15_out, isFibo, isSSUM, isGCD);
  or or_16 (or_16_out, GCD_equal, GCD_accA1, GCD_accB1, GCD_accBPrime, GCD_accAPrime);
  or or_17 (or_17_out, F11, FiboN__eq__eq__0);
  not not_7 (not_7_out, SS101);
  Sub #(.Bits(8)) sub_2 (.a(SP), .b(8'h1), .c_i(1'b0), .s(sub_2_s));  // open: c_o
  not not_8 (not_8_out, or_16_out);
  // NotConnected on notconnected_1_out
  not not_9 (not_9_out, or_17_out);
  // NotConnected on notconnected_2_out
  // NotConnected on notconnected_3_out
  or or_18 (or_18_out, reset, start);
  and and_22 (and_22_out, S1100, ~FiboN__eq__eq__0);  // And
  Multiplexer #(.Selector_Bits(4)) multiplexer_35 (
    .sel({Sa, Sb, Sc, Sd}), .in_0(1'b0), .in_1(1'b0), .in_2(or_15_out), .in_3(1'b0), .in_4(1'b0),
    .in_5(1'b0), .in_6(1'b0), .in_7(1'b0), .in_8(not_8_out), .in_9(1'b1), .in_10(1'b1),
    .in_11(notconnected_1_out), .in_12(not_9_out), .in_13(not_7_out), .in_14(notconnected_2_out),
    .in_15(notconnected_3_out), .out(multiplexer_35_out));
  or or_19 (or_19_out, SP_push, CALL);
  Decoder #(.Selector_Bits(2)) decoder_2 (.sel({FQa, FQb}), .out_0(F00), .out_1(F01), .out_2(F10), .out_3(F11));
  Multiplexer multiplexer_36 (.sel(reset), .in_0(multiplexer_35_out), .in_1(1'b0), .out(multiplexer_36_out));
  Multiplexer #(.Bits(8)) multiplexer_37 (.sel(and_23_out), .in_0(operand), .in_1(PC_rRAM), .out(multiplexer_37_out));
  and and_23 (and_23_out, _01, _1101);
  Add #(.Bits(8)) add_5 (.a(accA), .b(accB), .c_i(1'b0), .s(Sum));  // open: c_o
  Sub #(.Bits(8)) sub_3 (.a(accA), .b(accB), .c_i(1'b0), .s(Diff));  // open: c_o
  Mul #(.Bits(4)) mul_1 (.a(accA[3:0]), .b(accB[3:0]), .mul(Multy));
  Div #(.Bits(8)) div_1 (.a(accA), .b(accB), .q(quotient), .r(remain));
  not not_10 (not_10_out, FiboN__eq__eq__0);
  D_FF d_ff_5 (.D(multiplexer_36_out), .C(clk), .Q(Sa));  // open: nQ
  Add #(.Bits(8)) add_6 (.a(SP), .b(8'h1), .c_i(1'b0), .s(add_6_s));  // open: c_o
  Multiplexer #(.Selector_Bits(2)) multiplexer_38 (
    .sel({FQa, FQb}), .in_0(and_22_out), .in_1(not_10_out), .in_2(1'b1), .in_3(1'b0), .out(multiplexer_38_out));
  not not_11 (not_11_out, SS101);
  CounterPreset #(.Bits(8)) counterpreset_1 (
    .en(S0011), .C(clk), .dir(1'b0), .in(multiplexer_37_out), .ld(jump), .clr(S0000), .out(PC));  // open: ovf
  Multiplexer #(.Bits(8)) multiplexer_39 (.sel(reset), .in_0(A), .in_1({8{1'b0}}), .out(multiplexer_39_out));
  Multiplexer #(.Bits(8)) multiplexer_40 (.sel(reset), .in_0(B), .in_1({8{1'b0}}), .out(multiplexer_40_out));
  Multiplexer #(.Bits(8)) multiplexer_41 (.sel(or_19_out), .in_0({8{1'b0}}), .in_1(sub_2_s), .out(multiplexer_41_out));
  Multiplexer #(.Bits(8)) multiplexer_42 (
    .sel(or_25_out), .in_0(multiplexer_41_out), .in_1(add_6_s), .out(multiplexer_42_out));
  D_FF d_ff_6 (.D(multiplexer_38_out), .C(clk), .Q(FQb));  // open: nQ
  or or_20 (or_20_out, isFibo, isSSUM, useSP);
  or or_21 (or_21_out, F11, FiboN__eq__eq__0);
  not not_12 (not_12_out, progLoad);
  Multiplexer #(.Bits(8)) multiplexer_43 (
    .sel(or_18_out), .in_0(multiplexer_42_out), .in_1({8{1'b0}}), .out(multiplexer_43_out));
  or or_22 (loadN, F00, F01);
  or or_23 (loadFiboA, F00, F01);
  or or_24 (loadFiboB, F00, F01);
  // NotConnected on notconnected_4_out
  not not_13 (not_13_out, or_21_out);
  // NotConnected on notconnected_5_out
  // NotConnected on notconnected_6_out
  Counter #(.Bits(8)) counter_1 (.en(progLoad), .C(clk), .clr(not_12_out), .out(pRAM_Counter));  // open: ovf
  Register #(.Bits(8)) u_accA (.D(multiplexer_39_out), .C(clk), .en(load_accA), .Q(accA));
  Register #(.Bits(8)) u_accB (.D(multiplexer_40_out), .C(clk), .en(load_accB), .Q(accB));
  Multiplexer #(.Selector_Bits(4)) multiplexer_44 (
    .sel({Sa, Sb, Sc, Sd}), .in_0(result), .in_1(1'b0), .in_2(or_20_out), .in_3(1'b0), .in_4(1'b1),
    .in_5(1'b0), .in_6(rRAM_iter__lt__16), .in_7(1'b0), .in_8(1'b0), .in_9(1'b0), .in_10(1'b0),
    .in_11(notconnected_4_out), .in_12(not_13_out), .in_13(not_11_out), .in_14(notconnected_5_out),
    .in_15(notconnected_6_out), .out(multiplexer_44_out));
  Multiplexer #(.Bits(8)) multiplexer_45 (.sel(progLoad), .in_0(PC), .in_1(pRAM_Counter), .out(multiplexer_45_out));
  Multiplexer #(.Bits(8)) multiplexer_46 (
    .sel(accA_pRAMoperand), .in_0(multiplexer_45_out), .in_1(operand), .out(multiplexer_46_out));
  BarrelShifter #(.Bits(8)) barrelshifter_1 (.in(accA), .shift({1'b0, accB[2:0]}), .out(shiftLeft));
  BarrelShifter #(.Bits(8), .direction("right")) barrelshifter_2 (
    .in(accA), .shift({1'b0, accB[2:0]}), .out(shiftRight));
  BarrelShifter #(.Bits(8), .barrelShifterMode("rotate")) barrelshifter_3 (
    .in(accA), .shift({1'b0, accB[2:0]}), .out(rotateShiftLeft));
  BarrelShifter #(.Bits(8), .barrelShifterMode("rotate"), .direction("right")) barrelshifter_4 (
    .in(accA), .shift({1'b0, accB[2:0]}), .out(rotateShiftRight));
  Register #(.Bits(8)) u_SP (.D(multiplexer_43_out), .C(clk), .en(load_SP), .Q(SP));
  Multiplexer multiplexer_47 (.sel(reset), .in_0(multiplexer_44_out), .in_1(1'b0), .out(multiplexer_47_out));
  or or_25 (or_25_out, RET, SP_pop);
  D_FF d_ff_7 (.D(multiplexer_47_out), .C(clk), .Q(Sb));  // open: nQ
  RAMDualPort #(.AddrBits(8), .Bits(14)) pRAM (
    .A(multiplexer_46_out), .Din(progIn), .str(progLoad), .C(clk), .ld(not_14_out), .D({pRAM_d, out_12}));
  not not_14 (not_14_out, progLoad);
  or or_26 (or_26_out, F11, FiboN__eq__eq__0);
  Multiplexer #(.Bits(8)) multiplexer_48 (.sel(reset), .in_0(C), .in_1({8{1'b0}}), .out(multiplexer_48_out));
  Multiplexer #(.Bits(8)) multiplexer_49 (.sel(reset), .in_0(D), .in_1({8{1'b0}}), .out(multiplexer_49_out));
  assign \and  = accA & accB;  // And and_24, 8 bits wide
  assign \or  = accA | accB;  // Or or_27, 8 bits wide
  assign \xor  = accA ^ accB;  // XOr xor_1, 8 bits wide
  ROM #(.AddrBits(8)) isPrime_2 (.A(accB), .sel(1'b1), .D(isPrime_2_d));
  nor nor_1 (nor_1_out, useSP, isHALT, isSSUM, isFibo, isGCD);
  assign na = ~accA;  // Not not_15, 8 bits wide
  Comparator #(.Bits(8)) comparator_7 (
    .a(accA), .b(accB), .gt(comparator_7_gt), .eq(comparator_7_eq), .lt(comparator_7_lt));
  Comparator #(.Bits(8)) comparator_8 (.a(accA), .b(8'h1), .eq(comparator_8_eq));  // open: gt, lt
  and and_25 (GCD_accBPrime, isPrime_2_d, S1000);
  or or_28 (or_28_out, GCD_accB, GCD_equal, GCD_accA1, GCD_accB1, GCD_accBPrime, GCD_accAPrime);
  // NotConnected on notconnected_7_out
  // NotConnected on notconnected_8_out
  // NotConnected on notconnected_9_out
  Register #(.Bits(14)) IR (.D({pRAM_d, out_12}), .C(clk), .en(S0001), .Q({group, ALU, operand}));
  Register #(.Bits(8)) u_regC (.D(multiplexer_48_out), .C(clk), .en(load_regC), .Q(regC));
  Register #(.Bits(8)) u_regD (.D(multiplexer_49_out), .C(clk), .en(load_regD), .Q(regD));
  and and_26 (GCD_accA1, comparator_8_eq, S1000);
  Multiplexer #(.Selector_Bits(4)) multiplexer_50 (
    .sel({Sa, Sb, Sc, Sd}), .in_0(result), .in_1(1'b1), .in_2(nor_1_out), .in_3(1'b0), .in_4(1'b0),
    .in_5(1'b1), .in_6(rRAM_iter__lt__16), .in_7(1'b0), .in_8(or_28_out), .in_9(1'b0), .in_10(1'b0),
    .in_11(notconnected_7_out), .in_12(or_26_out), .in_13(SS101), .in_14(notconnected_8_out),
    .in_15(notconnected_9_out), .out(multiplexer_50_out));
  Multiplexer multiplexer_51 (.sel(reset), .in_0(multiplexer_50_out), .in_1(1'b0), .out(multiplexer_51_out));
  Seven_Seg_Hex seven_seg_hex_1 (.d(\output [7:4]), .dp(1'b0));
  and and_27 (GCD_accA, comparator_7_gt, S1000);
  and and_28 (GCD_equal, comparator_7_eq, S1000);
  and and_29 (GCD_accB, comparator_7_lt, S1000);
  Comparator #(.Bits(8)) comparator_9 (.a(accB), .b(8'h1), .eq(comparator_9_eq));  // open: gt, lt
  ROM #(.AddrBits(8)) isPrime_3 (.A(accA), .sel(1'b1), .D(isPrime_3_d));
  D_FF d_ff_8 (.D(multiplexer_51_out), .C(clk), .Q(Sc));  // open: nQ
  Seven_Seg_Hex seven_seg_hex_2 (.d(\output [3:0]), .dp(1'b0));
  and and_30 (GCD_accB1, comparator_9_eq, S1000);
  Decoder #(.Selector_Bits(2)) decoder_3 (.sel(group), .out_0(_00), .out_1(_01), .out_2(_10), .out_3(_11));
  and and_31 (GCD_accAPrime, isPrime_3_d, S1000);
  Multiplexer multiplexer_52 (.sel(reset_state), .in_0(reset), .in_1(reset_lt_16), .out(multiplexer_52_out));
  not not_16 (not_16_out, reset_lt_16);
  Sub #(.Bits(8)) sub_4 (.a(accB), .b(accA), .c_i(1'b0), .s(accB_GCD));  // open: c_o
  nor nor_2 (nor_2_out, useSP, isGCD, isFibo, isHALT);
  or or_29 (or_29_out, F11, FiboN__eq__eq__0);
  Decoder #(.Selector_Bits(4)) decoder_4 (
    .sel(ALU), .out_0(_0000), .out_1(_0001), .out_2(_0010), .out_3(_0011), .out_4(_0100), .out_5(_0101),
    .out_6(_0110), .out_7(_0111), .out_8(_1000), .out_9(_1001), .out_10(_1010), .out_11(_1011),
    .out_12(_1100), .out_13(_1101), .out_14(_1110), .out_15(_1111));
  Counter #(.Bits(8)) counter_2 (.en(S0110), .C(clk), .clr(S0000), .out(rRAM_Iter));  // open: ovf
  Comparator #(.Bits(8)) comparator_10 (.a(rRAM_Iter), .b(8'h10), .lt(rRAM_iter__lt__16));  // open: gt, eq
  D_FF d_ff_9 (.D(multiplexer_52_out), .C(clk), .Q(reset_state));  // open: nQ
  Counter #(.Bits(8)) counter_3 (.en(reset_state), .C(clk), .clr(not_16_out), .out(reset_iter));  // open: ovf
  Comparator #(.Bits(8)) comparator_11 (.a(reset_iter), .b(8'h10), .lt(reset_lt_16));  // open: gt, eq
  or or_30 (or_30_out, GCD_accA, GCD_equal, GCD_accA1, GCD_accB1, GCD_accBPrime, GCD_accAPrime);
  Multiplexer #(.Selector_Bits(4)) multiplexer_53 (
    .sel({Sa, Sb, Sc, Sd}), .in_0(start), .in_1(1'b0), .in_2(nor_2_out), .in_3(1'b1), .in_4(1'b1),
    .in_5(1'b1), .in_6(1'b0), .in_7(1'b0), .in_8(or_30_out), .in_9(1'b0), .in_10(1'b0),
    .in_11(notconnected_10_out), .in_12(or_29_out), .in_13(1'b1), .in_14(notconnected_11_out),
    .in_15(notconnected_12_out), .out(multiplexer_53_out));
  // NotConnected on notconnected_10_out
  // NotConnected on notconnected_11_out
  // NotConnected on notconnected_12_out
  Multiplexer multiplexer_54 (.sel(reset), .in_0(multiplexer_53_out), .in_1(1'b0), .out(multiplexer_54_out));
  D_FF d_ff_10 (.D(multiplexer_54_out), .C(clk), .Q(Sd));  // open: nQ
  Decoder #(.Selector_Bits(4)) decoder_5 (
    .sel({Sa, Sb, Sc, Sd}), .out_0(S0000), .out_1(S0001), .out_2(S0010), .out_3(S0011), .out_4(S0100),
    .out_5(S0101), .out_6(S0110), .out_7(S0111), .out_8(S1000), .out_9(S1001), .out_10(S1010),
    .out_11(S1011), .out_12(S1100), .out_13(S1101), .out_14(S1110), .out_15(S1111));
  or or_31 (load_valid, isHALT, S0001);
  and and_32 (isHALT, _11, S0010, _1111);
  or or_32 (or_32_out, _0000, _0100);
  and and_33 (accB_operand, _00, S0010, _0010);
  and and_34 (accB_accA, _00, S0010, _0101);
  and and_35 (regC_accA, _00, S0010, _0110);
  and and_36 (regC_M, _00, S0010, _1100);
  and and_37 (regD_accA, _00, S0010, _0111);
  and and_38 (regD_N, _00, S0010, _1101);
  and and_39 (jump_regD, _11, S0010, _0100);
  and and_40 (isFibo, _11, S0010, _1101);
  and and_41 (isGCD, _11, S0010, _1100);
  Register register_5 (.D(isHALT), .C(clk), .en(load_valid), .Q(valid));
  and and_42 (isSSUM, _11, S0010, _1110);
  and and_43 (and_43_out, _01, S0010, or_32_out);
  and and_44 (and_44_out, _1001, _01, S0100);
  or or_33 (Read_rRAM, and_45_out, and_43_out, and_44_out, and_46_out);
  or or_34 (load_regC, regC_accA, reset, regC_M);
  or or_35 (load_regD, regD_accA, regD_N, jump_regD, reset);
  or or_36 (or_36_out, accB_operand, reset, accB_accA);
  and and_45 (and_45_out, S1101, ~SS100, ~SS101);  // And
  and and_46 (and_46_out, _01, _1101, S0100);
  or or_37 (load_accB, or_36_out, S1010);
  and and_47 (CALL, _01, S0100, _1100);
  or or_38 (or_38_out, reset, start);
  and and_48 (RET, _01, S0101, _1101);
  and and_49 (rRAM_accA, _01, S0010, _0001);
  and and_50 (and_50_out, _01, S0010, _1100);
  and and_51 (and_51_out, _01, S0010, _1000);
  and and_52 (and_52_out, _01, S0010, _1001);
  and and_53 (and_53_out, _01, S0010, _1101);
  and and_54 (accA_operand, _00, S0010, _0001);
  and and_55 (accA_accB, _00, S0010, _0100);
  and and_56 (accA_regC, _00, S0010, _1000);
  and and_57 (accA_regD, _00, S0010, _1001);
  and and_58 (accA_SP, _00, S0010, _1010);
  and and_59 (accA_rRAMoperand, _01, S0010, _0000);
  and and_60 (accA_pRAMoperand, _01, S0010, _0010);
  and and_61 (accA_rRAMregC, _01, S0010, _0100);
  and and_62 (accA_rRAMSP, _01, S0100, _1001);
  and and_63 (SP_push, _01, S0100, _1000);
  and and_64 (SP_pop, _01, S0101, _1001);
  and and_65 (and_65_out, _01, S0100, _1101);
  and and_66 (and_66_out, _01, S0101, _1100);
  or or_39 (useSP, and_50_out, and_51_out, and_52_out, and_53_out);
  Multiplexer #(.Bits(8)) multiplexer_55 (.sel(GCD_accBPrime), .in_0({8{1'b0}}), .in_1(accB), .out(multiplexer_55_out));
  or or_40 (or_40_out, GCD_accB1, and_67_out);
  and and_67 (and_67_out, GCD_accAPrime, GCD_accBPrime);
  or or_41 (load_SP, CALL, SP_push, or_38_out, SP_pop, RET);
  and and_68 (and_68_out, _01, S0101, _1000);
  Multiplexer #(.Bits(8)) multiplexer_56 (
    .sel(or_40_out), .in_0(multiplexer_55_out), .in_1(8'h1), .out(multiplexer_56_out));
  and and_69 (and_69_out, _01, S0100, _1001);
  Multiplexer #(.Bits(8)) multiplexer_57 (
    .sel(S1001), .in_0(multiplexer_56_out), .in_1(Diff), .out(multiplexer_57_out));
  or or_42 (or_42_out, accA_operand, accA_accB, accA_regC, accA_regD, accA_SP, isPrime, accA_rRAMoperand, accA_pRAMoperand, accA_rRAMregC, accA_rRAMSP, and_74_out);
  and and_70 (and_70_out, _11, S0010, _1000);
  and and_71 (and_71_out, _11, S0010, _1000);
  and and_72 (and_72_out, _11, S0010, _1000);
  or or_43 (rRAM_SP, accA_rRAMSP, and_66_out, rRAM_accA, and_68_out, and_69_out, and_65_out);
  Multiplexer #(.Bits(8)) multiplexer_58 (
    .sel(isPrime), .in_0(multiplexer_57_out), .in_1({{7{1'b0}}, Prime[0]}), .out(multiplexer_58_out));
  and and_73 (isPrime, _11, S0010, _1001);
  Multiplexer #(.Bits(8)) multiplexer_59 (
    .sel(accA_rRAMSP), .in_0(multiplexer_58_out), .in_1(rRAM), .out(multiplexer_59_out));
  and and_74 (and_74_out, S0010, useALU);
  or or_44 (load_gr, and_70_out, reset);
  or or_45 (load_ls, and_71_out, reset);
  or or_46 (load_eq, and_72_out, isPrime, reset);
  Multiplexer #(.Bits(8)) multiplexer_60 (
    .sel(accA_rRAMregC), .in_0(multiplexer_59_out), .in_1(rRAM), .out(multiplexer_60_out));
  Multiplexer #(.Bits(8)) multiplexer_61 (
    .sel(accA_pRAMoperand), .in_0(multiplexer_60_out), .in_1(out_12), .out(multiplexer_61_out));
  Multiplexer #(.Bits(8)) multiplexer_62 (
    .sel(accA_rRAMoperand), .in_0(multiplexer_61_out), .in_1(rRAM), .out(multiplexer_62_out));
  Multiplexer #(.Bits(8)) multiplexer_63 (
    .sel(accA_SP), .in_0(multiplexer_62_out), .in_1(SP), .out(multiplexer_63_out));
  Multiplexer #(.Selector_Bits(4), .Bits(8)) multiplexer_64 (
    .sel(ALU), .in_0(Sum), .in_1(Diff), .in_2(Multy), .in_3({8{1'b0}}), .in_4(quotient), .in_5(remain),
    .in_6({8{1'b0}}), .in_7({8{1'b0}}), .in_8(\and ), .in_9(\or ), .in_10(\xor ), .in_11(na),
    .in_12(shiftLeft), .in_13(shiftRight), .in_14(rotateShiftLeft), .in_15(rotateShiftRight),
    .out(multiplexer_64_out));
  or or_47 (load_accA, S1001, reset, GCD_accBPrime, or_42_out, GCD_accB1);
  Multiplexer #(.Bits(8)) multiplexer_65 (
    .sel(accA_regD), .in_0(multiplexer_63_out), .in_1(regD), .out(multiplexer_65_out));
  Multiplexer #(.Bits(8)) multiplexer_66 (
    .sel(accA_regC), .in_0(multiplexer_65_out), .in_1(regC), .out(multiplexer_66_out));
  Multiplexer #(.Bits(8)) multiplexer_67 (
    .sel(accA_accB), .in_0(multiplexer_66_out), .in_1(accB), .out(multiplexer_67_out));
  Multiplexer #(.Bits(8)) multiplexer_68 (
    .sel(accA_operand), .in_0(multiplexer_67_out), .in_1(operand), .out(multiplexer_68_out));
  Multiplexer #(.Bits(8)) multiplexer_69 (.sel(useALU), .in_0(multiplexer_68_out), .in_1(multiplexer_64_out), .out(A));
  and and_75 (useALU, group[1], ~group[0]);  // And
  Multiplexer #(.Bits(8)) multiplexer_70 (.sel(S1010), .in_0({8{1'b0}}), .in_1(accB_GCD), .out(multiplexer_70_out));
  Sub #(.Bits(8)) sub_5 (.a(regD), .b(8'h1), .c_i(1'b0), .s(sub_5_s));  // open: c_o
  Multiplexer #(.Bits(8)) multiplexer_71 (
    .sel(accB_accA), .in_0(multiplexer_70_out), .in_1(accA), .out(multiplexer_71_out));
  Multiplexer #(.Bits(8)) multiplexer_72 (.sel(regC_M), .in_0({8{1'b0}}), .in_1(M), .out(multiplexer_72_out));
  Multiplexer #(.Bits(8)) multiplexer_73 (.sel(regC_accA), .in_0(multiplexer_72_out), .in_1(accA), .out(C));
  Multiplexer #(.Bits(8)) multiplexer_74 (.sel(accB_operand), .in_0(multiplexer_71_out), .in_1(operand), .out(B));
  Multiplexer #(.Bits(8)) multiplexer_75 (.sel(jump_regD), .in_0({8{1'b0}}), .in_1(sub_5_s), .out(multiplexer_75_out));
  Multiplexer #(.Bits(8)) multiplexer_76 (.sel(regD_N), .in_0(multiplexer_75_out), .in_1(N), .out(multiplexer_76_out));
  Multiplexer #(.Bits(8)) multiplexer_77 (.sel(regD_accA), .in_0(multiplexer_76_out), .in_1(accA), .out(D));

  // Other names for the same wires on the sheet: instruction[3:0] = ALU; opcode[5:0] = {group, ALU};
  //   accA_pRAMoperandValue[7:0] = out_12; n_t[4:0] = accA[4:0]; FiboA_7_0[7:0] = FiboA[7:0];
  //   FiboA_8_15[7:0] = FiboA[15:8]; FState[1:0] = {FQa, FQb}; rRAM_A_7_0 = F11; rRAM_A_15_8 = F10;
  //   State[3:0] = {Sa, Sb, Sc, Sd}; SSa = SS[2]; SSb = SS[1]; SSc = SS[0]; SSrRAM_7_0 = SS101; SSrRAM_15_8 = SS100;
  //   SSum_7_0[7:0] = SSum[7:0]; SSum_15_8[7:0] = SSum[15:8]; tPrime = Prime[0]

  // Notes on the sheet:
  //   rRAM Logic (wait for update)
  //   rRAM (done)
  //   jump (wait for update)
  //   Fibo Data Path (done)
  //   JumpPC
  //   flag (done i guess)
  //   contents of isPrime (hex, n*v repeats v):
  //   0,0,1,1,0,1,0,1,0,0,0,1,0,1,0,0,0,1,0,1,0,0,0,1,5*0,1,0,1,5*0
  //   ,1,0,0,0,1,0,1,0,0,0,1,5*0,1,5*0,1,0,1,5*0,1,0,0,0,1,0,1,5*0,1
  //   ,0,0,0,1,5*0,1,7*0,1,0,0,0,1,0,1,0,0,0,1,0,1,0,0,0,1,13*0,1,0,0,0
  //   ,1,5*0,1,0,1,9*0,1,0,1,5*0,1,5*0,1,0,0,0,1,5*0,1,5*0,1,0,1,9*0
  //   ,1,0,1,0,0,0,1,0,1,11*0,1,11*0,1,0,0,0,1,0,1,0,0,0,1,5*0,1,0,1
  //   ,9*0,1
  //   done output(done)
  //   Fibo Control Unit (done)
  //   Input (done)
  //   State (wait for update)
  //   SP (done i guess)
  //   Testcase (done??)
  //   pRAM (done)
  //   ALU (not done wait for update)
  //   Accumulator (done)
  //   GCD Logic (done)
  //   Register (done)
  //   Output
  //   contents of isPrime_2 (hex, n*v repeats v):
  //   0,0,1,1,0,1,0,1,0,0,0,1,0,1,0,0,0,1,0,1,0,0,0,1,5*0,1,0,1,5*0
  //   ,1,0,0,0,1,0,1,0,0,0,1,5*0,1,5*0,1,0,1,5*0,1,0,0,0,1,0,1,5*0,1
  //   ,0,0,0,1,5*0,1,7*0,1,0,0,0,1,0,1,0,0,0,1,0,1,0,0,0,1,13*0,1,0,0,0
  //   ,1,5*0,1,0,1,9*0,1,0,1,5*0,1,5*0,1,0,0,0,1,5*0,1,5*0,1,0,1,9*0
  //   ,1,0,1,0,0,0,1,0,1,11*0,1,11*0,1,0,0,0,1,0,1,0,0,0,1,5*0,1,0,1
  //   ,9*0,1
  //   contents of isPrime_3 (hex, n*v repeats v):
  //   0,0,1,1,0,1,0,1,0,0,0,1,0,1,0,0,0,1,0,1,0,0,0,1,5*0,1,0,1,5*0
  //   ,1,0,0,0,1,0,1,0,0,0,1,5*0,1,5*0,1,0,1,5*0,1,0,0,0,1,0,1,5*0,1
  //   ,0,0,0,1,5*0,1,7*0,1,0,0,0,1,0,1,0,0,0,1,0,1,0,0,0,1,13*0,1,0,0,0
  //   ,1,5*0,1,0,1,9*0,1,0,1,5*0,1,5*0,1,0,0,0,1,5*0,1,5*0,1,0,1,9*0
  //   ,1,0,1,0,0,0,1,0,1,11*0,1,11*0,1,0,0,0,1,0,1,0,0,0,1,5*0,1,0,1
  //   ,9*0,1
  //   Decode use for logic (done)
  //   rRAM Iterator (done)
  //   Clear Iterator (done)
  //   Control Unit (wait for update)
  //   newA (wait for update)
  //   newB (wait for update)
  //   newC (wait for update)
  //   newD (wait for update)
endmodule

/* Test case 01_P01T01:
M N progIn reset progLoad start result clk valid done output
0 0 0 0 0 0 0 0 x x x
0 0 0 0 0 0 0 1 x x x
0 0 0 1 0 0 0 0 x x x
0 0 0 1 0 0 0 1 0 0 x
0 0 0 0 0 0 0 0 0 x x
0 0 0 0 0 0 0 1 0 x x
0 0 0 0 0 0 0 0 0 x x
0 0 0 0 0 0 0 1 0 x x
0 0 0 0 0 0 0 0 0 x x
0 0 0 0 0 0 0 1 0 x x
0 0 0 0 0 0 0 0 0 x x
0 0 0 0 0 0 0 1 0 x x
0 0 0 0 0 0 0 0 0 x x
0 0 0 0 0 0 0 1 0 x x
0 0 0 0 0 0 0 0 0 x x
0 0 0 0 0 0 0 1 0 x x
0 0 0 0 0 0 0 0 0 x x
0 0 0 0 0 0 0 1 0 x x
0 0 0 0 0 0 0 0 0 x x
0 0 0 0 0 0 0 1 0 x x
0 0 0 0 0 0 0 0 0 x x
0 0 0 0 0 0 0 1 0 x x
0 0 0 0 0 0 0 0 0 x x
0 0 0 0 0 0 0 1 0 x x
0 0 0 0 0 0 0 0 0 x x
0 0 0 0 0 0 0 1 0 x x
0 0 0 0 0 0 0 0 0 x x
0 0 0 0 0 0 0 1 0 x x
0 0 0 0 0 0 0 0 0 x x
0 0 0 0 0 0 0 1 0 x x
0 0 0 0 0 0 0 0 0 x x
0 0 0 0 0 0 0 1 0 x x
0 0 0 0 0 0 0 0 0 x x
0 0 0 0 0 0 0 1 0 x x
0 0 0 0 0 0 0 0 0 x x
0 0 0 0 0 0 0 1 0 x x
0 0 0 0 0 0 0 0 0 x x
0 0 0 0 0 0 0 1 0 x x
0 0 0 0 0 0 0 0 0 x x
0 0 0 0 0 0 0 1 0 x x
0 0 0 0 0 0 0 0 0 x x
0 0 0 0 0 0 0 1 0 x x
0 0 0 0 0 0 0 0 0 x x
0 0 0 0 0 0 0 1 0 x x
0 0 271 0 1 0 0 0 0 x x
0 0 271 0 1 0 0 1 0 x x
0 0 565 0 1 0 0 0 0 x x
0 0 565 0 1 0 0 1 0 x x
0 0 8192 0 1 0 0 0 0 x x
0 0 8192 0 1 0 0 1 0 x x
0 0 4355 0 1 0 0 0 0 x x
0 0 4355 0 1 0 0 1 0 x x
0 0 16128 0 1 0 0 0 0 x x
0 0 16128 0 1 0 0 1 0 x x
0 0 0 0 0 1 0 0 x x x
0 0 0 0 0 1 0 1 x 0 x
0 0 0 0 0 0 0 0 x 0 x
0 0 0 0 0 0 0 1 x 0 x
0 0 0 0 0 0 0 0 x 0 x
0 0 0 0 0 0 0 1 x 0 x
0 0 0 0 0 0 0 0 x 0 x
0 0 0 0 0 0 0 1 x 0 x
0 0 0 0 0 0 0 0 x 0 x
0 0 0 0 0 0 0 1 x 0 x
0 0 0 0 0 0 0 0 x 0 x
0 0 0 0 0 0 0 1 x 0 x
0 0 0 0 0 0 0 0 x 0 x
0 0 0 0 0 0 0 1 x 0 x
0 0 0 0 0 0 0 0 x 0 x
0 0 0 0 0 0 0 1 x 0 x
0 0 0 0 0 0 0 0 x 0 x
0 0 0 0 0 0 0 1 x 0 x
0 0 0 0 0 0 0 0 x 0 x
0 0 0 0 0 0 0 1 x 0 x
0 0 0 0 0 0 0 0 x 0 x
0 0 0 0 0 0 0 1 x 0 x
0 0 0 0 0 0 0 0 x 0 x
0 0 0 0 0 0 0 1 x 0 x
0 0 0 0 0 0 0 0 x 0 x
0 0 0 0 0 0 0 1 x 0 x
0 0 0 0 0 0 0 0 x 0 x
0 0 0 0 0 0 0 1 x 0 x
0 0 0 0 0 0 0 0 x 0 x
0 0 0 0 0 0 0 1 x 0 x
0 0 0 0 0 0 0 0 x 0 x
0 0 0 0 0 0 0 1 x 0 x
0 0 0 0 0 0 0 0 x 0 x
0 0 0 0 0 0 0 1 x 0 x
0 0 0 0 0 0 0 0 x 0 x
0 0 0 0 0 0 0 1 x 0 x
0 0 0 0 0 0 0 0 x 0 x
0 0 0 0 0 0 0 1 x 0 x
0 0 0 0 0 0 0 0 x 0 x
0 0 0 0 0 0 0 1 x 0 x
0 0 0 0 0 0 0 0 x 0 x
0 0 0 0 0 0 0 1 x 0 x
0 0 0 0 0 0 0 0 x 0 x
0 0 0 0 0 0 0 1 x 0 x
0 0 0 0 0 0 0 0 x 0 x
0 0 0 0 0 0 0 1 x 0 x
0 0 0 0 0 0 0 0 x 0 x
0 0 0 0 0 0 0 1 x 0 x
0 0 0 0 0 0 0 0 x 0 x
0 0 0 0 0 0 0 1 1 0 x
0 0 0 0 0 0 1 0 1 x x
0 0 0 0 0 0 1 1 1 0 0
0 0 0 0 0 0 0 0 1 0 0
0 0 0 0 0 0 0 1 1 0 0
0 0 0 0 0 0 0 0 1 0 0
0 0 0 0 0 0 0 1 1 0 0
0 0 0 0 0 0 0 0 1 0 0
0 0 0 0 0 0 0 1 1 0 68
0 0 0 0 0 0 0 0 1 0 68
0 0 0 0 0 0 0 1 1 0 0
0 0 0 0 0 0 0 0 1 0 0
0 0 0 0 0 0 0 1 1 0 0
0 0 0 0 0 0 0 0 1 0 0
0 0 0 0 0 0 0 1 1 0 0
0 0 0 0 0 0 0 0 1 0 0
0 0 0 0 0 0 0 1 1 0 0
0 0 0 0 0 0 0 0 1 0 0
0 0 0 0 0 0 0 1 1 0 0
0 0 0 0 0 0 0 0 1 0 0
0 0 0 0 0 0 0 1 1 0 0
0 0 0 0 0 0 0 0 1 0 0
0 0 0 0 0 0 0 1 1 0 0
0 0 0 0 0 0 0 0 1 0 0
0 0 0 0 0 0 0 1 1 0 0
0 0 0 0 0 0 0 0 1 0 0
0 0 0 0 0 0 0 1 1 0 0
0 0 0 0 0 0 0 0 1 0 0
0 0 0 0 0 0 0 1 1 0 0
0 0 0 0 0 0 0 0 1 0 0
0 0 0 0 0 0 0 1 1 0 0
0 0 0 0 0 0 0 0 1 0 0
0 0 0 0 0 0 0 1 1 0 0
0 0 0 0 0 0 0 0 1 x 0
0 0 0 0 0 0 0 1 1 1 x
0 0 0 0 0 0 0 0 1 1 x
0 0 0 0 0 0 0 1 1 1 x
*/

/* Test case 11_P11T01:
M N progIn reset progLoad start result clk valid done output
0 0 0 0 0 0 0 0 x x x
0 0 0 0 0 0 0 1 x x x
0 0 0 1 0 0 0 0 x x x
0 0 0 1 0 0 0 1 0 0 x
0 0 0 0 0 0 0 0 0 x x
0 0 0 0 0 0 0 1 0 x x
0 0 0 0 0 0 0 0 0 x x
0 0 0 0 0 0 0 1 0 x x
0 0 0 0 0 0 0 0 0 x x
0 0 0 0 0 0 0 1 0 x x
0 0 0 0 0 0 0 0 0 x x
0 0 0 0 0 0 0 1 0 x x
0 0 0 0 0 0 0 0 0 x x
0 0 0 0 0 0 0 1 0 x x
0 0 0 0 0 0 0 0 0 x x
0 0 0 0 0 0 0 1 0 x x
0 0 0 0 0 0 0 0 0 x x
0 0 0 0 0 0 0 1 0 x x
0 0 0 0 0 0 0 0 0 x x
0 0 0 0 0 0 0 1 0 x x
0 0 0 0 0 0 0 0 0 x x
0 0 0 0 0 0 0 1 0 x x
0 0 0 0 0 0 0 0 0 x x
0 0 0 0 0 0 0 1 0 x x
0 0 0 0 0 0 0 0 0 x x
0 0 0 0 0 0 0 1 0 x x
0 0 0 0 0 0 0 0 0 x x
0 0 0 0 0 0 0 1 0 x x
0 0 0 0 0 0 0 0 0 x x
0 0 0 0 0 0 0 1 0 x x
0 0 0 0 0 0 0 0 0 x x
0 0 0 0 0 0 0 1 0 x x
0 0 0 0 0 0 0 0 0 x x
0 0 0 0 0 0 0 1 0 x x
0 0 0 0 0 0 0 0 0 x x
0 0 0 0 0 0 0 1 0 x x
0 0 0 0 0 0 0 0 0 x x
0 0 0 0 0 0 0 1 0 x x
0 0 0 0 0 0 0 0 0 x x
0 0 0 0 0 0 0 1 0 x x
0 0 0 0 0 0 0 0 0 x x
0 0 0 0 0 0 0 1 0 x x
0 0 0 0 0 0 0 0 0 x x
0 0 0 0 0 0 0 1 0 x x
0 0 3328 0 1 0 0 0 0 x x
0 0 3328 0 1 0 0 1 0 x x
0 0 256 0 1 0 0 0 0 x x
0 0 256 0 1 0 0 1 0 x x
0 0 1280 0 1 0 0 0 0 x x
0 0 1280 0 1 0 0 1 0 x x
0 0 2304 0 1 0 0 0 0 x x
0 0 2304 0 1 0 0 1 0 x x
0 0 8192 0 1 0 0 0 0 x x
0 0 8192 0 1 0 0 1 0 x x
0 0 13314 0 1 0 0 0 0 x x
0 0 13314 0 1 0 0 1 0 x x
0 0 4352 0 1 0 0 0 0 x x
0 0 4352 0 1 0 0 1 0 x x
0 0 2304 0 1 0 0 0 0 x x
0 0 2304 0 1 0 0 1 0 x x
0 0 4353 0 1 0 0 0 0 x x
0 0 4353 0 1 0 0 1 0 x x
0 0 16128 0 1 0 0 0 0 x x
0 0 16128 0 1 0 0 1 0 x x
0 10 0 0 0 1 0 0 x x x
0 10 0 0 0 1 0 1 x 0 x
0 10 0 0 0 0 0 0 x 0 x
0 10 0 0 0 0 0 1 x 0 x
0 10 0 0 0 0 0 0 x 0 x
0 10 0 0 0 0 0 1 x 0 x
0 10 0 0 0 0 0 0 x 0 x
0 10 0 0 0 0 0 1 x 0 x
0 10 0 0 0 0 0 0 x 0 x
0 10 0 0 0 0 0 1 x 0 x
0 10 0 0 0 0 0 0 x 0 x
0 10 0 0 0 0 0 1 x 0 x
0 10 0 0 0 0 0 0 x 0 x
0 10 0 0 0 0 0 1 x 0 x
0 10 0 0 0 0 0 0 x 0 x
0 10 0 0 0 0 0 1 x 0 x
0 10 0 0 0 0 0 0 x 0 x
0 10 0 0 0 0 0 1 x 0 x
0 10 0 0 0 0 0 0 x 0 x
0 10 0 0 0 0 0 1 x 0 x
0 10 0 0 0 0 0 0 x 0 x
0 10 0 0 0 0 0 1 x 0 x
0 10 0 0 0 0 0 0 x 0 x
0 10 0 0 0 0 0 1 x 0 x
0 10 0 0 0 0 0 0 x 0 x
0 10 0 0 0 0 0 1 x 0 x
0 10 0 0 0 0 0 0 x 0 x
0 10 0 0 0 0 0 1 x 0 x
0 10 0 0 0 0 0 0 x 0 x
0 10 0 0 0 0 0 1 x 0 x
0 10 0 0 0 0 0 0 x 0 x
0 10 0 0 0 0 0 1 x 0 x
0 10 0 0 0 0 0 0 x 0 x
0 10 0 0 0 0 0 1 x 0 x
0 10 0 0 0 0 0 0 x 0 x
0 10 0 0 0 0 0 1 x 0 x
0 10 0 0 0 0 0 0 x 0 x
0 10 0 0 0 0 0 1 x 0 x
0 10 0 0 0 0 0 0 x 0 x
0 10 0 0 0 0 0 1 x 0 x
0 10 0 0 0 0 0 0 x 0 x
0 10 0 0 0 0 0 1 x 0 x
0 10 0 0 0 0 0 0 x 0 x
0 10 0 0 0 0 0 1 x 0 x
0 10 0 0 0 0 0 0 x 0 x
0 10 0 0 0 0 0 1 x 0 x
0 10 0 0 0 0 0 0 x 0 x
0 10 0 0 0 0 0 1 x 0 x
0 10 0 0 0 0 0 0 x 0 x
0 10 0 0 0 0 0 1 x 0 x
0 10 0 0 0 0 0 0 x 0 x
0 10 0 0 0 0 0 1 x 0 x
0 10 0 0 0 0 0 0 x 0 x
0 10 0 0 0 0 0 1 x 0 x
0 10 0 0 0 0 0 0 x 0 x
0 10 0 0 0 0 0 1 x 0 x
0 10 0 0 0 0 0 0 x 0 x
0 10 0 0 0 0 0 1 x 0 x
0 10 0 0 0 0 0 0 x 0 x
0 10 0 0 0 0 0 1 x 0 x
0 10 0 0 0 0 0 0 x 0 x
0 10 0 0 0 0 0 1 x 0 x
0 10 0 0 0 0 0 0 x 0 x
0 10 0 0 0 0 0 1 x 0 x
0 10 0 0 0 0 0 0 x 0 x
0 10 0 0 0 0 0 1 x 0 x
0 10 0 0 0 0 0 0 x 0 x
0 10 0 0 0 0 0 1 x 0 x
0 10 0 0 0 0 0 0 x 0 x
0 10 0 0 0 0 0 1 x 0 x
0 10 0 0 0 0 0 0 x 0 x
0 10 0 0 0 0 0 1 x 0 x
0 10 0 0 0 0 0 0 x 0 x
0 10 0 0 0 0 0 1 x 0 x
0 10 0 0 0 0 0 0 x 0 x
0 10 0 0 0 0 0 1 x 0 x
0 10 0 0 0 0 0 0 x 0 x
0 10 0 0 0 0 0 1 x 0 x
0 10 0 0 0 0 0 0 x 0 x
0 10 0 0 0 0 0 1 x 0 x
0 10 0 0 0 0 0 0 x 0 x
0 10 0 0 0 0 0 1 x 0 x
0 10 0 0 0 0 0 0 x 0 x
0 10 0 0 0 0 0 1 x 0 x
0 10 0 0 0 0 0 0 x 0 x
0 10 0 0 0 0 0 1 x 0 x
0 10 0 0 0 0 0 0 x 0 x
0 10 0 0 0 0 0 1 x 0 x
0 10 0 0 0 0 0 0 x 0 x
0 10 0 0 0 0 0 1 x 0 x
0 10 0 0 0 0 0 0 x 0 x
0 10 0 0 0 0 0 1 x 0 x
0 10 0 0 0 0 0 0 x 0 x
0 10 0 0 0 0 0 1 x 0 x
0 10 0 0 0 0 0 0 x 0 x
0 10 0 0 0 0 0 1 x 0 x
0 10 0 0 0 0 0 0 x 0 x
0 10 0 0 0 0 0 1 x 0 x
0 10 0 0 0 0 0 0 x 0 x
0 10 0 0 0 0 0 1 x 0 x
0 10 0 0 0 0 0 0 x 0 x
0 10 0 0 0 0 0 1 x 0 x
0 10 0 0 0 0 0 0 x 0 x
0 10 0 0 0 0 0 1 x 0 x
0 10 0 0 0 0 0 0 x 0 x
0 10 0 0 0 0 0 1 x 0 x
0 10 0 0 0 0 0 0 x 0 x
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*/

/* Test case 21_P08T02:
M N progIn reset progLoad start result clk valid done output
0 0 0 0 0 0 0 C x x x
0 0 0 1 0 0 0 C 0 0 x
repeat(20) 0 0 0 0 0 0 0 C 0 x x
0 0 456 0 1 0 0 C 0 x x
0 0 519 0 1 0 0 C 0 x x
0 0 9216 0 1 0 0 C 0 x x
0 0 4352 0 1 0 0 C 0 x x
0 0 456 0 1 0 0 C 0 x x
0 0 9472 0 1 0 0 C 0 x x
0 0 4353 0 1 0 0 C 0 x x
0 0 384 0 1 0 0 C 0 x x
0 0 515 0 1 0 0 C 0 x x
0 0 9216 0 1 0 0 C 0 x x
0 0 4354 0 1 0 0 C 0 x x
0 0 511 0 1 0 0 C 0 x x
0 0 767 0 1 0 0 C 0 x x
0 0 9472 0 1 0 0 C 0 x x
0 0 4355 0 1 0 0 C 0 x x
0 0 261 0 1 0 0 C 0 x x
0 0 521 0 1 0 0 C 0 x x
0 0 9216 0 1 0 0 C 0 x x
0 0 4356 0 1 0 0 C 0 x x
0 0 16128 0 1 0 0 C 0 x x
0 0 0 0 0 1 0 C x 0 x
repeat(83) 0 0 0 0 0 0 0 C x 0 x
0 0 0 0 0 0 0 C 1 0 x
0 0 0 0 0 0 1 C 1 0 28
0 0 0 0 0 0 0 C 1 0 4
0 0 0 0 0 0 0 C 1 0 42
repeat(13) 0 0 0 0 0 0 0 C 1 0 0
repeat(2) 0 0 0 0 0 0 0 C 1 1 x
*/

/* Test case 02_P02T01:
M N progIn reset progLoad start result clk valid done output
0 0 0 0 0 0 0 0 x x x
0 0 0 0 0 0 0 1 x x x
0 0 0 1 0 0 0 0 x x x
0 0 0 1 0 0 0 1 0 0 x
0 0 0 0 0 0 0 0 0 x x
0 0 0 0 0 0 0 1 0 x x
0 0 0 0 0 0 0 0 0 x x
0 0 0 0 0 0 0 1 0 x x
0 0 0 0 0 0 0 0 0 x x
0 0 0 0 0 0 0 1 0 x x
0 0 0 0 0 0 0 0 0 x x
0 0 0 0 0 0 0 1 0 x x
0 0 0 0 0 0 0 0 0 x x
0 0 0 0 0 0 0 1 0 x x
0 0 0 0 0 0 0 0 0 x x
0 0 0 0 0 0 0 1 0 x x
0 0 0 0 0 0 0 0 0 x x
0 0 0 0 0 0 0 1 0 x x
0 0 0 0 0 0 0 0 0 x x
0 0 0 0 0 0 0 1 0 x x
0 0 0 0 0 0 0 0 0 x x
0 0 0 0 0 0 0 1 0 x x
0 0 0 0 0 0 0 0 0 x x
0 0 0 0 0 0 0 1 0 x x
0 0 0 0 0 0 0 0 0 x x
0 0 0 0 0 0 0 1 0 x x
0 0 0 0 0 0 0 0 0 x x
0 0 0 0 0 0 0 1 0 x x
0 0 0 0 0 0 0 0 0 x x
0 0 0 0 0 0 0 1 0 x x
0 0 0 0 0 0 0 0 0 x x
0 0 0 0 0 0 0 1 0 x x
0 0 0 0 0 0 0 0 0 x x
0 0 0 0 0 0 0 1 0 x x
0 0 0 0 0 0 0 0 0 x x
0 0 0 0 0 0 0 1 0 x x
0 0 0 0 0 0 0 0 0 x x
0 0 0 0 0 0 0 1 0 x x
0 0 0 0 0 0 0 0 0 x x
0 0 0 0 0 0 0 1 0 x x
0 0 0 0 0 0 0 0 0 x x
0 0 0 0 0 0 0 1 0 x x
0 0 0 0 0 0 0 0 0 x x
0 0 0 0 0 0 0 1 0 x x
0 0 257 0 1 0 0 0 0 x x
0 0 257 0 1 0 0 1 0 x x
0 0 12291 0 1 0 0 0 0 x x
0 0 12291 0 1 0 0 1 0 x x
0 0 355 0 1 0 0 0 0 x x
0 0 355 0 1 0 0 1 0 x x
0 0 4352 0 1 0 0 0 0 x x
0 0 4352 0 1 0 0 1 0 x x
0 0 258 0 1 0 0 0 0 x x
0 0 258 0 1 0 0 1 0 x x
0 0 12295 0 1 0 0 0 0 x x
0 0 12295 0 1 0 0 1 0 x x
0 0 16128 0 1 0 0 0 0 x x
0 0 16128 0 1 0 0 1 0 x x
0 0 4353 0 1 0 0 0 0 x x
0 0 4353 0 1 0 0 1 0 x x
0 0 16128 0 1 0 0 0 0 x x
0 0 16128 0 1 0 0 1 0 x x
0 0 0 0 0 1 0 0 x x x
0 0 0 0 0 1 0 1 x 0 x
0 0 0 0 0 0 0 0 x 0 x
0 0 0 0 0 0 0 1 x 0 x
0 0 0 0 0 0 0 0 x 0 x
0 0 0 0 0 0 0 1 x 0 x
0 0 0 0 0 0 0 0 x 0 x
0 0 0 0 0 0 0 1 x 0 x
0 0 0 0 0 0 0 0 x 0 x
0 0 0 0 0 0 0 1 x 0 x
0 0 0 0 0 0 0 0 x 0 x
0 0 0 0 0 0 0 1 x 0 x
0 0 0 0 0 0 0 0 x 0 x
0 0 0 0 0 0 0 1 x 0 x
0 0 0 0 0 0 0 0 x 0 x
0 0 0 0 0 0 0 1 x 0 x
0 0 0 0 0 0 0 0 x 0 x
0 0 0 0 0 0 0 1 x 0 x
0 0 0 0 0 0 0 0 x 0 x
0 0 0 0 0 0 0 1 x 0 x
0 0 0 0 0 0 0 0 x 0 x
0 0 0 0 0 0 0 1 x 0 x
0 0 0 0 0 0 0 0 x 0 x
0 0 0 0 0 0 0 1 x 0 x
0 0 0 0 0 0 0 0 x 0 x
0 0 0 0 0 0 0 1 x 0 x
0 0 0 0 0 0 0 0 x 0 x
0 0 0 0 0 0 0 1 x 0 x
0 0 0 0 0 0 0 0 x 0 x
0 0 0 0 0 0 0 1 x 0 x
0 0 0 0 0 0 0 0 x 0 x
0 0 0 0 0 0 0 1 x 0 x
0 0 0 0 0 0 0 0 x 0 x
0 0 0 0 0 0 0 1 x 0 x
0 0 0 0 0 0 0 0 x 0 x
0 0 0 0 0 0 0 1 x 0 x
0 0 0 0 0 0 0 0 x 0 x
0 0 0 0 0 0 0 1 x 0 x
0 0 0 0 0 0 0 0 x 0 x
0 0 0 0 0 0 0 1 x 0 x
0 0 0 0 0 0 0 0 x 0 x
0 0 0 0 0 0 0 1 x 0 x
0 0 0 0 0 0 0 0 x 0 x
0 0 0 0 0 0 0 1 x 0 x
0 0 0 0 0 0 0 0 x 0 x
0 0 0 0 0 0 0 1 x 0 x
0 0 0 0 0 0 0 0 x 0 x
0 0 0 0 0 0 0 1 x 0 x
0 0 0 0 0 0 0 0 x 0 x
0 0 0 0 0 0 0 1 x 0 x
0 0 0 0 0 0 0 0 x 0 x
0 0 0 0 0 0 0 1 x 0 x
0 0 0 0 0 0 0 0 x 0 x
0 0 0 0 0 0 0 1 x 0 x
0 0 0 0 0 0 0 0 x 0 x
0 0 0 0 0 0 0 1 x 0 x
0 0 0 0 0 0 0 0 x 0 x
0 0 0 0 0 0 0 1 x 0 x
0 0 0 0 0 0 0 0 x 0 x
0 0 0 0 0 0 0 1 x 0 x
0 0 0 0 0 0 0 0 x 0 x
0 0 0 0 0 0 0 1 x 0 x
0 0 0 0 0 0 0 0 x 0 x
0 0 0 0 0 0 0 1 x 0 x
0 0 0 0 0 0 0 0 x 0 x
0 0 0 0 0 0 0 1 1 0 x
0 0 0 0 0 0 1 0 1 x x
0 0 0 0 0 0 1 1 1 0 1
0 0 0 0 0 0 0 0 1 0 1
0 0 0 0 0 0 0 1 1 0 2
0 0 0 0 0 0 0 0 1 0 2
0 0 0 0 0 0 0 1 1 0 0
0 0 0 0 0 0 0 0 1 0 0
0 0 0 0 0 0 0 1 1 0 0
0 0 0 0 0 0 0 0 1 0 0
0 0 0 0 0 0 0 1 1 0 0
0 0 0 0 0 0 0 0 1 0 0
0 0 0 0 0 0 0 1 1 0 0
0 0 0 0 0 0 0 0 1 0 0
0 0 0 0 0 0 0 1 1 0 0
0 0 0 0 0 0 0 0 1 0 0
0 0 0 0 0 0 0 1 1 0 0
0 0 0 0 0 0 0 0 1 0 0
0 0 0 0 0 0 0 1 1 0 0
0 0 0 0 0 0 0 0 1 0 0
0 0 0 0 0 0 0 1 1 0 0
0 0 0 0 0 0 0 0 1 0 0
0 0 0 0 0 0 0 1 1 0 0
0 0 0 0 0 0 0 0 1 0 0
0 0 0 0 0 0 0 1 1 0 0
0 0 0 0 0 0 0 0 1 0 0
0 0 0 0 0 0 0 1 1 0 0
0 0 0 0 0 0 0 0 1 0 0
0 0 0 0 0 0 0 1 1 0 0
0 0 0 0 0 0 0 0 1 0 0
0 0 0 0 0 0 0 1 1 0 0
0 0 0 0 0 0 0 0 1 0 0
0 0 0 0 0 0 0 1 1 0 0
0 0 0 0 0 0 0 0 1 x 0
0 0 0 0 0 0 0 1 1 1 x
0 0 0 0 0 0 0 0 1 1 x
0 0 0 0 0 0 0 1 1 1 x
*/

/* Test case 12_P12T01:
M N progIn reset progLoad start result clk valid done output
0 0 0 0 0 0 0 0 x x x
0 0 0 0 0 0 0 1 x x x
0 0 0 1 0 0 0 0 x x x
0 0 0 1 0 0 0 1 0 0 x
0 0 0 0 0 0 0 0 0 x x
0 0 0 0 0 0 0 1 0 x x
0 0 0 0 0 0 0 0 0 x x
0 0 0 0 0 0 0 1 0 x x
0 0 0 0 0 0 0 0 0 x x
0 0 0 0 0 0 0 1 0 x x
0 0 0 0 0 0 0 0 0 x x
0 0 0 0 0 0 0 1 0 x x
0 0 0 0 0 0 0 0 0 x x
0 0 0 0 0 0 0 1 0 x x
0 0 0 0 0 0 0 0 0 x x
0 0 0 0 0 0 0 1 0 x x
0 0 0 0 0 0 0 0 0 x x
0 0 0 0 0 0 0 1 0 x x
0 0 0 0 0 0 0 0 0 x x
0 0 0 0 0 0 0 1 0 x x
0 0 0 0 0 0 0 0 0 x x
0 0 0 0 0 0 0 1 0 x x
0 0 0 0 0 0 0 0 0 x x
0 0 0 0 0 0 0 1 0 x x
0 0 0 0 0 0 0 0 0 x x
0 0 0 0 0 0 0 1 0 x x
0 0 0 0 0 0 0 0 0 x x
0 0 0 0 0 0 0 1 0 x x
0 0 0 0 0 0 0 0 0 x x
0 0 0 0 0 0 0 1 0 x x
0 0 0 0 0 0 0 0 0 x x
0 0 0 0 0 0 0 1 0 x x
0 0 0 0 0 0 0 0 0 x x
0 0 0 0 0 0 0 1 0 x x
0 0 0 0 0 0 0 0 0 x x
0 0 0 0 0 0 0 1 0 x x
0 0 0 0 0 0 0 0 0 x x
0 0 0 0 0 0 0 1 0 x x
0 0 0 0 0 0 0 0 0 x x
0 0 0 0 0 0 0 1 0 x x
0 0 0 0 0 0 0 0 0 x x
0 0 0 0 0 0 0 1 0 x x
0 0 0 0 0 0 0 0 0 x x
0 0 0 0 0 0 0 1 0 x x
0 0 268 0 1 0 0 0 0 x x
0 0 268 0 1 0 0 1 0 x x
0 0 530 0 1 0 0 0 0 x x
0 0 530 0 1 0 0 1 0 x x
0 0 15360 0 1 0 0 0 0 x x
0 0 15360 0 1 0 0 1 0 x x
0 0 4352 0 1 0 0 0 0 x x
0 0 4352 0 1 0 0 1 0 x x
0 0 356 0 1 0 0 0 0 x x
0 0 356 0 1 0 0 1 0 x x
0 0 587 0 1 0 0 0 0 x x
0 0 587 0 1 0 0 1 0 x x
0 0 15360 0 1 0 0 0 0 x x
0 0 15360 0 1 0 0 1 0 x x
0 0 4353 0 1 0 0 0 0 x x
0 0 4353 0 1 0 0 1 0 x x
0 0 273 0 1 0 0 0 0 x x
0 0 273 0 1 0 0 1 0 x x
0 0 517 0 1 0 0 0 0 x x
0 0 517 0 1 0 0 1 0 x x
0 0 15360 0 1 0 0 0 0 x x
0 0 15360 0 1 0 0 1 0 x x
0 0 4354 0 1 0 0 0 0 x x
0 0 4354 0 1 0 0 1 0 x x
0 0 304 0 1 0 0 0 0 x x
0 0 304 0 1 0 0 1 0 x x
0 0 560 0 1 0 0 0 0 x x
0 0 560 0 1 0 0 1 0 x x
0 0 15360 0 1 0 0 0 0 x x
0 0 15360 0 1 0 0 1 0 x x
0 0 4355 0 1 0 0 0 0 x x
0 0 4355 0 1 0 0 1 0 x x
0 0 1024 0 1 0 0 0 0 x x
0 0 1024 0 1 0 0 1 0 x x
0 0 4367 0 1 0 0 0 0 x x
0 0 4367 0 1 0 0 1 0 x x
0 0 16128 0 1 0 0 0 0 x x
0 0 16128 0 1 0 0 1 0 x x
0 0 0 0 0 1 0 0 x x x
0 0 0 0 0 1 0 1 x 0 x
0 0 0 0 0 0 0 0 x 0 x
0 0 0 0 0 0 0 1 x 0 x
0 0 0 0 0 0 0 0 x 0 x
0 0 0 0 0 0 0 1 x 0 x
0 0 0 0 0 0 0 0 x 0 x
0 0 0 0 0 0 0 1 x 0 x
0 0 0 0 0 0 0 0 x 0 x
0 0 0 0 0 0 0 1 x 0 x
0 0 0 0 0 0 0 0 x 0 x
0 0 0 0 0 0 0 1 x 0 x
0 0 0 0 0 0 0 0 x 0 x
0 0 0 0 0 0 0 1 x 0 x
0 0 0 0 0 0 0 0 x 0 x
0 0 0 0 0 0 0 1 x 0 x
0 0 0 0 0 0 0 0 x 0 x
0 0 0 0 0 0 0 1 x 0 x
0 0 0 0 0 0 0 0 x 0 x
0 0 0 0 0 0 0 1 x 0 x
0 0 0 0 0 0 0 0 x 0 x
0 0 0 0 0 0 0 1 x 0 x
0 0 0 0 0 0 0 0 x 0 x
0 0 0 0 0 0 0 1 x 0 x
0 0 0 0 0 0 0 0 x 0 x
0 0 0 0 0 0 0 1 x 0 x
0 0 0 0 0 0 0 0 x 0 x
0 0 0 0 0 0 0 1 x 0 x
0 0 0 0 0 0 0 0 x 0 x
0 0 0 0 0 0 0 1 x 0 x
0 0 0 0 0 0 0 0 x 0 x
0 0 0 0 0 0 0 1 x 0 x
0 0 0 0 0 0 0 0 x 0 x
0 0 0 0 0 0 0 1 x 0 x
0 0 0 0 0 0 0 0 x 0 x
0 0 0 0 0 0 0 1 x 0 x
0 0 0 0 0 0 0 0 x 0 x
0 0 0 0 0 0 0 1 x 0 x
0 0 0 0 0 0 0 0 x 0 x
0 0 0 0 0 0 0 1 x 0 x
0 0 0 0 0 0 0 0 x 0 x
0 0 0 0 0 0 0 1 x 0 x
0 0 0 0 0 0 0 0 x 0 x
0 0 0 0 0 0 0 1 x 0 x
0 0 0 0 0 0 0 0 x 0 x
0 0 0 0 0 0 0 1 x 0 x
0 0 0 0 0 0 0 0 x 0 x
0 0 0 0 0 0 0 1 x 0 x
0 0 0 0 0 0 0 0 x 0 x
0 0 0 0 0 0 0 1 x 0 x
0 0 0 0 0 0 0 0 x 0 x
0 0 0 0 0 0 0 1 x 0 x
0 0 0 0 0 0 0 0 x 0 x
0 0 0 0 0 0 0 1 x 0 x
0 0 0 0 0 0 0 0 x 0 x
0 0 0 0 0 0 0 1 x 0 x
0 0 0 0 0 0 0 0 x 0 x
0 0 0 0 0 0 0 1 x 0 x
0 0 0 0 0 0 0 0 x 0 x
0 0 0 0 0 0 0 1 x 0 x
0 0 0 0 0 0 0 0 x 0 x
0 0 0 0 0 0 0 1 x 0 x
0 0 0 0 0 0 0 0 x 0 x
0 0 0 0 0 0 0 1 x 0 x
0 0 0 0 0 0 0 0 x 0 x
0 0 0 0 0 0 0 1 x 0 x
0 0 0 0 0 0 0 0 x 0 x
0 0 0 0 0 0 0 1 x 0 x
0 0 0 0 0 0 0 0 x 0 x
0 0 0 0 0 0 0 1 x 0 x
0 0 0 0 0 0 0 0 x 0 x
0 0 0 0 0 0 0 1 x 0 x
0 0 0 0 0 0 0 0 x 0 x
0 0 0 0 0 0 0 1 x 0 x
0 0 0 0 0 0 0 0 x 0 x
0 0 0 0 0 0 0 1 x 0 x
0 0 0 0 0 0 0 0 x 0 x
0 0 0 0 0 0 0 1 x 0 x
0 0 0 0 0 0 0 0 x 0 x
0 0 0 0 0 0 0 1 x 0 x
0 0 0 0 0 0 0 0 x 0 x
0 0 0 0 0 0 0 1 x 0 x
0 0 0 0 0 0 0 0 x 0 x
0 0 0 0 0 0 0 1 x 0 x
0 0 0 0 0 0 0 0 x 0 x
0 0 0 0 0 0 0 1 x 0 x
0 0 0 0 0 0 0 0 x 0 x
0 0 0 0 0 0 0 1 x 0 x
0 0 0 0 0 0 0 0 x 0 x
0 0 0 0 0 0 0 1 x 0 x
0 0 0 0 0 0 0 0 x 0 x
0 0 0 0 0 0 0 1 x 0 x
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*/

/* Test case 22_P09T02:
M N progIn reset progLoad start result clk valid done output
0 0 0 0 0 0 0 C x x x
0 0 0 1 0 0 0 C 0 0 x
repeat(20) 0 0 0 0 0 0 0 C 0 x x
0 0 435 0 1 0 0 C 0 x x
0 0 515 0 1 0 0 C 0 x x
0 0 11264 0 1 0 0 C 0 x x
0 0 4352 0 1 0 0 C 0 x x
0 0 435 0 1 0 0 C 0 x x
0 0 515 0 1 0 0 C 0 x x
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*/

/* Test case 03_P03T01:
M N progIn reset progLoad start result clk valid done output
0 0 0 0 0 0 0 0 x x x
0 0 0 0 0 0 0 1 x x x
0 0 0 1 0 0 0 0 x x x
0 0 0 1 0 0 0 1 0 0 x
0 0 0 0 0 0 0 0 0 x x
0 0 0 0 0 0 0 1 0 x x
0 0 0 0 0 0 0 0 0 x x
0 0 0 0 0 0 0 1 0 x x
0 0 0 0 0 0 0 0 0 x x
0 0 0 0 0 0 0 1 0 x x
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*/

/* Test case 13_P13T01:
M N progIn reset progLoad start result clk valid done output
0 0 0 0 0 0 0 0 x x x
0 0 0 0 0 0 0 1 x x x
0 0 0 1 0 0 0 0 x x x
0 0 0 1 0 0 0 1 0 0 x
0 0 0 0 0 0 0 0 0 x x
0 0 0 0 0 0 0 1 0 x x
0 0 0 0 0 0 0 0 0 x x
0 0 0 0 0 0 0 1 0 x x
0 0 0 0 0 0 0 0 0 x x
0 0 0 0 0 0 0 1 0 x x
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*/

/* Test case 23_P10T02:
M N progIn reset progLoad start result clk valid done output
0 0 0 0 0 0 0 C x x x
0 0 0 1 0 0 0 C 0 0 x
repeat(20) 0 0 0 0 0 0 0 C 0 x x
0 0 264 0 1 0 0 C 0 x x
0 0 1792 0 1 0 0 C 0 x x
0 0 273 0 1 0 0 C 0 x x
0 0 6144 0 1 0 0 C 0 x x
0 0 529 0 1 0 0 C 0 x x
0 0 8192 0 1 0 0 C 0 x x
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*/

/* Test case 04_P04T01:
M N progIn reset progLoad start result clk valid done output
0 0 0 0 0 0 0 0 x x x
0 0 0 0 0 0 0 1 x x x
0 0 0 1 0 0 0 0 x x x
0 0 0 1 0 0 0 1 0 0 x
0 0 0 0 0 0 0 0 0 x x
0 0 0 0 0 0 0 1 0 x x
0 0 0 0 0 0 0 0 0 x x
0 0 0 0 0 0 0 1 0 x x
0 0 0 0 0 0 0 0 0 x x
0 0 0 0 0 0 0 1 0 x x
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*/

/* Test case 14_P01T02:
M N progIn reset progLoad start result clk valid done output
0 0 0 0 0 0 0 C x x x
0 0 0 1 0 0 0 C 0 0 x
repeat(20) 0 0 0 0 0 0 0 C 0 x x
0 0 346 0 1 0 0 C 0 x x
0 0 4352 0 1 0 0 C 0 x x
0 0 677 0 1 0 0 C 0 x x
0 0 1024 0 1 0 0 C 0 x x
0 0 4367 0 1 0 0 C 0 x x
0 0 375 0 1 0 0 C 0 x x
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*/

/* Test case 24_P11T02:
M N progIn reset progLoad start result clk valid done output
0 0 0 0 0 0 0 C x x x
0 0 0 1 0 0 0 C 0 0 x
repeat(20) 0 0 0 0 0 0 0 C 0 x x
0 0 256 0 1 0 0 C 0 x x
0 0 1536 0 1 0 0 C 0 x x
0 0 259 0 1 0 0 C 0 x x
0 0 1792 0 1 0 0 C 0 x x
0 0 2304 0 1 0 0 C 0 x x
0 0 6144 0 1 0 0 C 0 x x
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*/

/* Test case 05_P05T01:
M N progIn reset progLoad start result clk valid done output
0 0 0 0 0 0 0 0 x x x
0 0 0 0 0 0 0 1 x x x
0 0 0 1 0 0 0 0 x x x
0 0 0 1 0 0 0 1 0 0 x
0 0 0 0 0 0 0 0 0 x x
0 0 0 0 0 0 0 1 0 x x
0 0 0 0 0 0 0 0 0 x x
0 0 0 0 0 0 0 1 0 x x
0 0 0 0 0 0 0 0 0 x x
0 0 0 0 0 0 0 1 0 x x
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*/

/* Test case 15_P02T02:
M N progIn reset progLoad start result clk valid done output
0 0 0 0 0 0 0 C x x x
0 0 0 1 0 0 0 C 0 0 x
repeat(20) 0 0 0 0 0 0 0 C 0 x x
0 0 496 0 1 0 0 C 0 x x
0 0 517 0 1 0 0 C 0 x x
0 0 14336 0 1 0 0 C 0 x x
0 0 13061 0 1 0 0 C 0 x x
0 0 256 0 1 0 0 C 0 x x
0 0 4352 0 1 0 0 C 0 x x
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*/

/* Test case 25_P12T02:
M N progIn reset progLoad start result clk valid done output
0 0 0 0 0 0 0 C x x x
0 0 0 1 0 0 0 C 0 0 x
repeat(20) 0 0 0 0 0 0 0 C 0 x x
0 0 511 0 1 0 0 C 0 x x
0 0 513 0 1 0 0 C 0 x x
0 0 15360 0 1 0 0 C 0 x x
0 0 4352 0 1 0 0 C 0 x x
0 0 257 0 1 0 0 C 0 x x
0 0 767 0 1 0 0 C 0 x x
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*/

/* Test case 06_P06T01:
M N progIn reset progLoad start result clk valid done output
0 0 0 0 0 0 0 0 x x x
0 0 0 0 0 0 0 1 x x x
0 0 0 1 0 0 0 0 x x x
0 0 0 1 0 0 0 1 0 0 x
0 0 0 0 0 0 0 0 0 x x
0 0 0 0 0 0 0 1 0 x x
0 0 0 0 0 0 0 0 0 x x
0 0 0 0 0 0 0 1 0 x x
0 0 0 0 0 0 0 0 0 x x
0 0 0 0 0 0 0 1 0 x x
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*/

/* Test case 16_P03T02:
M N progIn reset progLoad start result clk valid done output
0 0 0 0 0 0 0 C x x x
0 0 0 1 0 0 0 C 0 0 x
repeat(20) 0 0 0 0 0 0 0 C 0 x x
0 0 4628 0 1 0 0 C 0 x x
0 0 4352 0 1 0 0 C 0 x x
0 0 4629 0 1 0 0 C 0 x x
0 0 4353 0 1 0 0 C 0 x x
0 0 4630 0 1 0 0 C 0 x x
0 0 4354 0 1 0 0 C 0 x x
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*/

/* Test case 26_P13T02:
M N progIn reset progLoad start result clk valid done output
0 0 0 0 0 0 0 C x x x
0 0 0 1 0 0 0 C 0 0 x
repeat(20) 0 0 0 0 0 0 0 C 0 x x
0 0 280 0 1 0 0 C 0 x x
0 0 15616 0 1 0 0 C 0 x x
0 0 4106 0 1 0 0 C 0 x x
0 0 4352 0 1 0 0 C 0 x x
0 0 4107 0 1 0 0 C 0 x x
0 0 4353 0 1 0 0 C 0 x x
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*/

/* Test case 07_P07T01:
M N progIn reset progLoad start result clk valid done output
0 0 0 0 0 0 0 0 x x x
0 0 0 0 0 0 0 1 x x x
0 0 0 1 0 0 0 0 x x x
0 0 0 1 0 0 0 1 0 0 x
0 0 0 0 0 0 0 0 0 x x
0 0 0 0 0 0 0 1 0 x x
0 0 0 0 0 0 0 0 0 x x
0 0 0 0 0 0 0 1 0 x x
0 0 0 0 0 0 0 0 0 x x
0 0 0 0 0 0 0 1 0 x x
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*/

/* Test case 17_P04T02:
M N progIn reset progLoad start result clk valid done output
0 0 0 0 0 0 0 C x x x
0 0 0 1 0 0 0 C 0 0 x
repeat(20) 0 0 0 0 0 0 0 C 0 x x
0 0 256 0 1 0 0 C 0 x x
0 0 14592 0 1 0 0 C 0 x x
0 0 256 0 1 0 0 C 0 x x
0 0 12549 0 1 0 0 C 0 x x
0 0 12294 0 1 0 0 C 0 x x
0 0 257 0 1 0 0 C 0 x x
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*/

/* Test case 27_P13T4:
M N progIn reset progLoad start result clk valid done output
0 0      0     0        0     0      0   0     x    x      x
0 0      0     0        0     0      0   1     x    x      x
0 0      0     1        0     0      0   0     x    x      x
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*/

/* Test case 08_P08T01:
M N progIn reset progLoad start result clk valid done output
0 0 0 0 0 0 0 0 x x x
0 0 0 0 0 0 0 1 x x x
0 0 0 1 0 0 0 0 x x x
0 0 0 1 0 0 0 1 0 0 x
0 0 0 0 0 0 0 0 0 x x
0 0 0 0 0 0 0 1 0 x x
0 0 0 0 0 0 0 0 0 x x
0 0 0 0 0 0 0 1 0 x x
0 0 0 0 0 0 0 0 0 x x
0 0 0 0 0 0 0 1 0 x x
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*/

/* Test case 18_P05T02:
M N progIn reset progLoad start result clk valid done output
0 0 0 0 0 0 0 C x x x
0 0 0 1 0 0 0 C 0 0 x
repeat(20) 0 0 0 0 0 0 0 C 0 x x
0 0 260 0 1 0 0 C 0 x x
0 0 516 0 1 0 0 C 0 x x
0 0 14336 0 1 0 0 C 0 x x
0 0 14592 0 1 0 0 C 0 x x
0 0 12569 0 1 0 0 C 0 x x
0 0 257 0 1 0 0 C 0 x x
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*/

/* Test case 28_P13T5:
M N progIn reset progLoad start result clk valid done output
0 0      0     0        0     0      0   0     x    x      x
0 0      0     0        0     0      0   1     x    x      x
0 0      0     1        0     0      0   0     x    x      x
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*/

/* Test case 09_P09T01:
M N progIn reset progLoad start result clk valid done output
0 0 0 0 0 0 0 0 x x x
0 0 0 0 0 0 0 1 x x x
0 0 0 1 0 0 0 0 x x x
0 0 0 1 0 0 0 1 0 0 x
0 0 0 0 0 0 0 0 0 x x
0 0 0 0 0 0 0 1 0 x x
0 0 0 0 0 0 0 0 0 x x
0 0 0 0 0 0 0 1 0 x x
0 0 0 0 0 0 0 0 0 x x
0 0 0 0 0 0 0 1 0 x x
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*/

/* Test case 19_P06T02:
M N progIn reset progLoad start result clk valid done output
0 0 0 0 0 0 0 C x x x
0 0 0 1 0 0 0 C 0 0 x
repeat(20) 0 0 0 0 0 0 0 C 0 x x
0 0 3072 0 1 0 0 C 0 x x
0 0 3328 0 1 0 0 C 0 x x
0 0 2048 0 1 0 0 C 0 x x
0 0 4352 0 1 0 0 C 0 x x
0 0 2304 0 1 0 0 C 0 x x
0 0 4353 0 1 0 0 C 0 x x
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*/

/* Test case 29_P13T6:
M N progIn reset progLoad start result clk valid done output
0 0      0     0        0     0      0   0     x    x      x
0 0      0     0        0     0      0   1     x    x      x
0 0      0     1        0     0      0   0     x    x      x
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*/

/* Test case 10_P10T01:
M N progIn reset progLoad start result clk valid done output
0 0 0 0 0 0 0 0 x x x
0 0 0 0 0 0 0 1 x x x
0 0 0 1 0 0 0 0 x x x
0 0 0 1 0 0 0 1 0 0 x
0 0 0 0 0 0 0 0 0 x x
0 0 0 0 0 0 0 1 0 x x
0 0 0 0 0 0 0 0 0 x x
0 0 0 0 0 0 0 1 0 x x
0 0 0 0 0 0 0 0 0 x x
0 0 0 0 0 0 0 1 0 x x
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*/

/* Test case 20_P07T02:
M N progIn reset progLoad start result clk valid done output
0 0 0 0 0 0 0 C x x x
0 0 0 1 0 0 0 C 0 0 x
repeat(20) 0 0 0 0 0 0 0 C 0 x x
0 0 320 0 1 0 0 C 0 x x
0 0 1536 0 1 0 0 C 0 x x
0 0 264 0 1 0 0 C 0 x x
0 0 1792 0 1 0 0 C 0 x x
0 0 259 0 1 0 0 C 0 x x
0 0 5376 0 1 0 0 C 0 x x
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*/
