// Digital circuit 1_02_Template.dig as structural Verilog
module _1_02_Template (
  input  A,
  input  B,
  output And,
  output Or,
  output Nand,
  output Nor,
  output Xor,
  output Xnor
);

  and and_1 (And, A, B);
  or or_1 (Or, A, B);
  nand nand_1 (Nand, A, B);
  nor nor_1 (Nor, A, B);
  xor xor_1 (Xor, A, B);
  xnor xnor_1 (Xnor, A, B);
endmodule
