// Digital circuit 2_04Template.dig as structural Verilog
module _2_04Template (
  input  A,
  input  B,
  input  Cin,
  output Sum,
  output Cout
);

  wire not_1_out, not_2_out, not_3_out, not_4_out, not_5_out, not_6_out, not_7_out, not_8_out, or_1_out,
       or_2_out, or_3_out, or_4_out, or_5_out, or_6_out, or_7_out;

  not not_1 (not_1_out, B);
  not not_2 (not_2_out, Cin);
  not not_3 (not_3_out, A);
  not not_4 (not_4_out, Cin);
  not not_5 (not_5_out, A);
  not not_6 (not_6_out, A);
  not not_7 (not_7_out, B);
  not not_8 (not_8_out, B);
  or or_1 (or_1_out, A, not_1_out, not_2_out);
  or or_2 (or_2_out, not_3_out, B, not_4_out);
  or or_3 (or_3_out, not_5_out, not_7_out, Cin);
  or or_4 (or_4_out, A, B, Cin);
  or or_5 (or_5_out, A, B);
  or or_6 (or_6_out, A, not_8_out, Cin);
  or or_7 (or_7_out, not_6_out, B, Cin);
  and and_1 (Sum, or_1_out, or_2_out, or_3_out, or_4_out);
  and and_2 (Cout, or_5_out, or_6_out, or_7_out);
endmodule
