// Digital circuit 2_08Template.dig as structural Verilog
module _2_08Template (
  input  X0,
  input  X1,
  input  Selector,
  output Z
);

  wire not_1_out, not_2_out, not_3_out, or_1_out, or_2_out, or_3_out, or_4_out;

  not not_1 (not_1_out, X0);
  not not_2 (not_2_out, X1);
  not not_3 (not_3_out, Selector);
  or or_1 (or_1_out, X0, X1, Selector);
  or or_2 (or_2_out, X0, not_2_out, Selector);
  or or_3 (or_3_out, X0, X1, not_3_out);
  or or_4 (or_4_out, not_1_out, X1, not_3_out);
  and and_1 (Z, or_1_out, or_2_out, or_3_out, or_4_out);
endmodule
