// Digital circuit 3_03Template.dig as structural Verilog
module _3_03Template (
  input  [3:0] In,
  input  [1:0] Selector,
  output [3:0] Output
);

  wire and_1_out, and_2_out, and_3_out, and_4_out, and_5_out, and_6_out, and_7_out, and_8_out, and_9_out,
       and_10_out, and_11_out, and_12_out, and_13_out, and_14_out, and_15_out, and_16_out, and_17_out,
       and_18_out, and_19_out, not_1_out, not_2_out, not_3_out, not_4_out, not_5_out, not_6_out, not_7_out,
       not_8_out, not_9_out, not_10_out, not_11_out, not_12_out, not_13_out, not_14_out, not_15_out,
       not_16_out, not_17_out, not_18_out, not_19_out, not_20_out;
  wire [2:0] Cyclic;
  wire [3:0] Excess_3;
  wire [3:1] _2_4_2_1, _6_4_2__3;

  not not_1 (not_1_out, In[0]);
  not not_2 (not_2_out, In[1]);
  not not_3 (not_3_out, In[0]);
  not not_4 (not_4_out, In[2]);
  not not_5 (not_5_out, In[3]);
  not not_6 (not_6_out, In[2]);
  not not_7 (not_7_out, In[3]);
  not not_8 (not_8_out, In[0]);
  not not_9 (not_9_out, In[1]);
  and and_1 (and_1_out, not_1_out, not_2_out);
  and and_2 (and_2_out, not_3_out, In[1]);
  and and_3 (and_3_out, In[0], In[1]);
  and and_4 (and_4_out, In[0], In[3]);
  and and_5 (and_5_out, In[0], not_4_out, not_5_out);
  and and_6 (and_6_out, In[1], not_6_out, not_7_out);
  and and_7 (and_7_out, not_8_out, In[2], not_9_out);
  or or_1 (Excess_3[0], and_1_out, and_2_out);
  or or_2 (Excess_3[1], and_1_out, and_3_out);
  or or_3 (Excess_3[2], and_4_out, and_5_out, and_6_out, and_7_out);
  and and_8 (and_8_out, In[0], In[2]);
  and and_9 (and_9_out, In[1], In[2]);
  not not_10 (not_10_out, In[2]);
  and and_10 (and_10_out, In[3], not_10_out);
  or or_4 (Excess_3[3], and_8_out, and_9_out, and_10_out);
  not not_11 (not_11_out, In[0]);
  not not_12 (not_12_out, In[1]);
  not not_13 (not_13_out, In[1]);
  not not_14 (not_14_out, In[2]);
  not not_15 (not_15_out, In[3]);
  Multiplexer #(.Selector_Bits(2), .Bits(4)) multiplexer_1 (
    .sel(Selector), .in_0(Excess_3), .in_1({In[3], Cyclic}), .in_2({_2_4_2_1, In[0]}),
    .in_3({_6_4_2__3, In[0]}), .out(Output));
  and and_11 (and_11_out, not_11_out, In[1]);
  and and_12 (and_12_out, In[0], not_12_out);
  and and_13 (and_13_out, In[2], not_13_out);
  and and_14 (and_14_out, not_14_out, not_15_out, In[1]);
  or or_5 (Cyclic[0], and_11_out, and_12_out);
  or or_6 (Cyclic[1], and_13_out, and_14_out);
  or or_7 (Cyclic[2], In[2], and_10_out);
  not not_16 (not_16_out, In[2]);
  not not_17 (not_17_out, In[1]);
  and and_15 (and_15_out, In[0], In[1]);
  and and_16 (and_16_out, In[0], not_16_out, not_17_out);
  or or_8 (_6_4_2__3[1], and_11_out, In[3], and_17_out);
  or or_9 (_6_4_2__3[2], and_19_out, and_18_out, and_16_out);
  or or_10 (_6_4_2__3[3], and_8_out, and_15_out, In[3]);
  not not_18 (not_18_out, In[1]);
  not not_19 (not_19_out, In[0]);
  not not_20 (not_20_out, In[1]);
  and and_17 (and_17_out, In[0], not_18_out, In[2]);
  and and_18 (and_18_out, not_19_out, not_20_out, In[2]);
  and and_19 (and_19_out, In[2], In[1]);
  or or_11 (_2_4_2_1[1], and_10_out, and_6_out, and_17_out);
  or or_12 (_2_4_2_1[2], and_18_out, In[3], and_19_out);
  or or_13 (_2_4_2_1[3], In[3], and_19_out, and_8_out);

  // Other names for the same wires on the sheet: _2_4_2_1[0] = In[0]; _6_4_2__3[0] = In[0]; A = In[0]; B = In[1];
  //   C = In[2]; Cyclic[3] = In[3]; D = In[3]
endmodule
