// Digital circuit 3_04Template.dig as structural Verilog
module _3_04Template (
  input  [6:0] In,
  output [6:0] Output
);

  wire _0, _1, _2, _3, _4, _5, _6, C1, C2, C3;

  xor xor_1 (C1, In[6], In[4], In[2], In[0]);
  xor xor_2 (C2, In[5], In[4], In[1], In[0]);
  xor xor_3 (C3, In[3], In[2], In[1], In[0]);
  Decoder #(.Selector_Bits(3)) decoder_1 (
    .sel({C3, C2, C1}), .out_1(_6), .out_2(_5), .out_3(_4), .out_4(_3), .out_5(_2), .out_6(_1), .out_7(_0));  // open: out_0
  assign Output = {_6, _5, _4, _3, _2, _1, _0} ^ In;  // XOr xor_4, 7 bits wide

  // Other names for the same wires on the sheet: I7 = In[0]; I6 = In[1]; I5 = In[2]; I4 = In[3]; I3 = In[4];
  //   I2 = In[5]; I1 = In[6]
endmodule
