// Digital circuit 6_01Template.dig as structural Verilog
module _6_01Template (
  input  reset,
  input  clk,
  output A,
  output B,
  output C
);

  wire and_1_out, and_2_out, and_3_out, and_4_out, xnor_1_out;

  D_FF d_ff_1 (.D(and_1_out), .C(clk), .Q(C));  // open: nQ
  and and_1 (and_1_out, ~reset, A);  // And
  and and_2 (and_2_out, ~reset, xnor_1_out);  // And
  D_FF d_ff_2 (.D(and_2_out), .C(clk), .Q(B));  // open: nQ
  xnor xnor_1 (xnor_1_out, C, A);
  and and_3 (and_3_out, ~reset, and_4_out);  // And
  D_FF d_ff_3 (.D(and_3_out), .C(clk), .Q(A));  // open: nQ
  and and_4 (and_4_out, ~C, B);  // And
endmodule
