// Digital circuit 6_02Template.dig as structural Verilog
module _6_02Template (
  input  reset,
  input  X,
  input  Y,
  input  Z,
  input  load,
  input  clock,
  output A,
  output B,
  output C
);

  wire and_1_out, and_2_out, and_3_out, and_4_out, and_5_out, and_6_out, and_7_out, and_8_out, and_9_out,
       and_10_out, and_11_out, and_12_out, and_13_out, and_14_out, or_1_out, or_2_out, or_3_out, or_4_out,
       or_5_out, or_6_out;

  and and_1 (and_1_out, ~reset, or_1_out);  // And
  or or_1 (or_1_out, and_2_out, and_4_out);
  and and_2 (and_2_out, load, X);
  and and_3 (and_3_out, ~A, C);  // And
  D_FF d_ff_1 (.D(and_1_out), .C(clock), .Q(A));  // open: nQ
  and and_4 (and_4_out, or_2_out, ~load);  // And
  or or_2 (or_2_out, and_3_out, and_5_out, and_6_out);
  and and_5 (and_5_out, ~B, C);  // And
  and and_6 (and_6_out, A, B, ~C);  // And
  D_FF d_ff_2 (.D(and_7_out), .C(clock), .Q(B));  // open: nQ
  and and_7 (and_7_out, ~reset, or_3_out);  // And
  or or_3 (or_3_out, and_8_out, and_9_out);
  and and_8 (and_8_out, load, Y);
  or or_4 (or_4_out, ~C, and_10_out);  // Or
  and and_9 (and_9_out, or_4_out, ~load);  // And
  and and_10 (and_10_out, A, ~B);  // And
  and and_11 (and_11_out, ~reset, or_5_out);  // And
  and and_12 (and_12_out, load, Z);
  D_FF d_ff_3 (.D(and_11_out), .C(clock), .Q(C));  // open: nQ
  or or_5 (or_5_out, and_12_out, and_13_out);
  and and_13 (and_13_out, or_6_out, ~load);  // And
  or or_6 (or_6_out, B, and_14_out);
  and and_14 (and_14_out, A, C);

  // Other names for the same wires on the sheet: CK = clock; L = load; R = reset
endmodule

/* Test case T06:
X Y Z reset load clock A B C
0 0 0 1 0 0 x x x
0 0 0 1 0 1 0 0 0
1 1 0 0 1 0 0 0 0
1 1 0 0 1 1 1 1 0
0 0 0 0 0 0 1 1 0
0 0 0 0 0 1 1 1 1
0 0 0 0 0 0 1 1 1
0 0 0 0 0 1 0 0 1
0 0 0 0 0 0 0 0 1
0 0 0 0 0 1 1 0 0
0 0 0 0 0 0 1 0 0
0 0 0 0 0 1 0 1 0
0 0 0 0 0 0 0 1 0
0 0 0 0 0 1 0 1 1
0 0 0 0 0 0 0 1 1
0 0 0 0 0 1 1 0 1
0 0 0 0 0 0 1 0 1
0 0 0 0 0 1 1 1 1
0 0 0 0 0 0 1 1 1
0 0 0 0 0 1 0 0 1
0 0 0 0 0 0 0 0 1
*/
