// Digital circuit 6_03Template.dig as structural Verilog
module _6_03Template (
  input  reset,
  input  [1:0] Coin,
  input  clock,
  output Open,
  output [3:0] Change
);

  wire and_1_out, and_2_out, and_3_out, and_4_out, and_5_out, and_7_out, and_8_out, and_9_out, and_10_out,
       multiplexer_1_out, multiplexer_2_out, multiplexer_3_out, nor_1_out, nor_2_out, not_1_out, or_1_out,
       xor_1_out;
  wire [1:0] S;
  wire [3:0] multiplexer_4_out;

  and and_1 (and_1_out, Coin[1], ~Coin[0]);  // And
  and and_2 (and_2_out, Coin[0], ~Coin[1]);  // And
  nor nor_1 (nor_1_out, Coin[0], Coin[1]);
  Multiplexer #(.Selector_Bits(2)) multiplexer_1 (
    .sel(S), .in_0(and_1_out), .in_1(and_2_out), .in_2(nor_1_out), .in_3(nor_1_out), .out(multiplexer_1_out));
  and and_3 (and_3_out, ~reset, multiplexer_1_out);  // And
  xor xor_1 (xor_1_out, Coin[1], Coin[0]);
  nor nor_2 (nor_2_out, Coin[1], Coin[0]);
  D_FF d_ff_1 (.D(and_3_out), .C(clock), .Q(S[1]));  // open: nQ
  and and_4 (and_4_out, ~reset, multiplexer_2_out);  // And
  Multiplexer #(.Selector_Bits(2)) multiplexer_2 (
    .sel(S), .in_0(xor_1_out), .in_1(nor_2_out), .in_2(1'b0), .in_3(nor_2_out), .out(multiplexer_2_out));
  D_FF d_ff_2 (.D(and_4_out), .C(clock), .Q(S[0]));  // open: nQ
  and and_5 (and_5_out, Coin[0], Coin[1]);
  or or_1 (or_1_out, Coin[0], Coin[1]);
  and and_6 (Open, ~reset, multiplexer_3_out);  // And
  Multiplexer #(.Selector_Bits(2)) multiplexer_3 (
    .sel(S), .in_0(and_5_out), .in_1(Coin[1]), .in_2(or_1_out), .in_3(or_1_out), .out(multiplexer_3_out));
  and and_7 (and_7_out, Coin[1], ~Coin[0]);  // And
  and and_8 (and_8_out, Coin[1], Coin[0]);
  and and_9 (and_9_out, Coin[1], ~Coin[0]);  // And
  and and_10 (and_10_out, Coin[1], Coin[0]);
  Multiplexer #(.Selector_Bits(2)) multiplexer_4 (
    .sel(S), .in_0(1'b0), .in_1(and_7_out), .in_2(and_7_out), .in_3(Coin[0]), .out(multiplexer_4_out[0]));
  Multiplexer #(.Selector_Bits(2)) multiplexer_5 (
    .sel(S), .in_0(1'b0), .in_1(and_8_out), .in_2(and_9_out), .in_3(1'b0), .out(multiplexer_4_out[1]));
  Multiplexer #(.Selector_Bits(2)) multiplexer_6 (
    .sel(S), .in_0(and_10_out), .in_1(and_10_out), .in_2(1'b0), .in_3(and_9_out), .out(multiplexer_4_out[2]));
  Multiplexer #(.Selector_Bits(2)) multiplexer_7 (
    .sel(S), .in_0(1'b0), .in_1(1'b0), .in_2(and_10_out), .in_3(and_10_out), .out(multiplexer_4_out[3]));
  Multiplexer #(.Bits(4)) multiplexer_8 (.sel(not_1_out), .in_0(4'b0000), .in_1(multiplexer_4_out), .out(Change));
  not not_1 (not_1_out, reset);

  // Other names for the same wires on the sheet: CK = clock; C0 = Coin[0]; C1 = Coin[1]; R = reset
endmodule

/* Test case T14:
reset Coin clock Open Change
1 0 0 x x
1 0 1 x x
1 0 0 0 0
1 0 1 x x
1 0 0 0 0
1 0 1 x x
1 0 0 0 0
1 0 1 x x
0 0 0 0 0
0 0 1 x x
0 0 0 0 0
0 0 1 x x
0 0 0 0 0
0 0 1 x x
0 0 0 0 0
0 0 1 x x
0 0 0 0 0
0 0 1 x x
0 0 0 0 0
0 0 1 x x
0 1 0 0 0
0 1 1 x x
0 1 0 0 0
0 1 1 x x
0 2 0 1 3
0 2 1 x x
0 0 0 0 0
0 0 1 x x
0 0 0 0 0
0 0 1 x x
0 0 0 0 0
0 0 1 x x
0 0 0 0 0
0 0 1 x x
1 0 0 0 0
1 0 1 x x
1 0 0 0 0
1 0 1 x x
0 0 0 0 0
0 0 1 x x
0 0 0 0 0
0 0 1 x x
0 2 0 0 0
0 2 1 x x
0 3 0 1 9
0 3 1 x x
0 0 0 0 0
0 0 1 x x
*/

/* Test case T12:
reset Coin clock Open Change
1 0 0 x x
1 0 1 x x
0 1 0 0 0
0 1 1 x x
1 0 0 0 0
1 0 1 x x
0 0 0 0 0
0 0 1 x x
0 1 0 0 0
0 1 1 x x
0 1 0 0 0
0 1 1 x x
1 0 0 0 0
1 0 1 x x
0 0 0 0 0
0 0 1 x x
0 2 0 0 0
0 2 1 x x
1 0 0 0 0
1 0 1 x x
0 0 0 0 0
0 0 1 x x
0 1 0 0 0
0 1 1 x x
0 1 0 0 0
0 1 1 x x
0 1 0 1 0
0 1 1 x x
0 0 0 0 0
0 0 1 x x
0 2 0 0 0
0 2 1 x x
0 0 0 0 0
0 0 1 x x
1 0 0 0 0
1 0 1 x x
0 3 0 1 4
0 3 1 x x
0 0 0 0 0
0 0 1 x x
*/

/* Test case T10:
reset Coin clock Open Change
1 0 0 x x
1 0 1 x x
0 0 0 0 0
0 0 1 x x
0 0 0 0 0
0 0 1 x x
0 1 0 0 0
0 1 1 x x
0 0 0 0 0
0 0 1 x x
0 0 0 0 0
0 0 1 x x
0 1 0 0 0
0 1 1 x x
0 0 0 0 0
0 0 1 x x
0 0 0 0 0
0 0 1 x x
0 0 0 0 0
0 0 1 x x
0 2 0 1 3
0 2 1 x x
0 0 0 0 0
0 0 1 x x
0 0 0 0 0
0 0 1 x x
0 2 0 0 0
0 2 1 x x
0 0 0 0 0
0 0 1 x x
0 0 0 0 0
0 0 1 x x
0 3 0 1 9
0 3 1 x x
0 0 0 0 0
0 0 1 x x
0 1 0 0 0
0 1 1 x x
0 0 0 0 0
0 0 1 x x
0 2 0 1 1
0 2 1 x x
0 0 0 0 0
0 0 1 x x
0 0 0 0 0
0 0 1 x x
*/

/* Test case T09:
reset Coin clock Open Change
1 0 0 x x
1 0 1 x x
0 1 0 0 0
0 1 1 x x
0 1 0 0 0
0 1 1 x x
0 3 0 1 8
0 3 1 x x
0 0 0 0 0
0 0 1 x x
0 0 0 0 0
0 0 1 x x
*/

/* Test case T07:
reset Coin clock Open Change
1 0 0 x x
1 0 1 x x
0 1 0 0 0
0 1 1 x x
0 1 0 0 0
0 1 1 x x
0 1 0 1 0
0 1 1 x x
0 0 0 0 0
0 0 1 x x
0 0 0 0 0
0 0 1 x x
*/

/* Test case T05:
reset Coin clock Open Change
1 0 0 x x
1 0 1 x x
0 1 0 0 0
0 1 1 x x
0 2 0 1 1
0 2 1 x x
0 0 0 0 0
0 0 1 x x
0 0 0 0 0
0 0 1 x x
*/

/* Test case T02:
reset Coin clock Open Change
1 0 0 x x
1 0 1 x x
0 2 0 0 0
0 2 1 x x
0 1 0 1 1
0 1 1 x x
0 0 0 0 0
0 0 1 x x
0 0 0 0 0
0 0 1 x x
*/

/* Test case T01:
reset Coin clock Open Change
1 0 0 x x
1 0 1 x x
0 3 0 1 4
0 3 1 x x
0 0 0 0 0
0 0 1 x x
0 0 0 0 0
0 0 1 x x
*/
