// Digital circuit 6_04Template.dig as structural Verilog
module _6_04Template (
  input  reset,
  input  [1:0] Coin,
  input  clock,
  output Open,
  output [3:0] Change,
  output [3:0] S
);

  wire A, and_1_out, and_2_out, and_4_out, and_8_out, and_9_out, multiplexer_1_out, multiplexer_2_out,
       multiplexer_3_out, multiplexer_4_out, not_2_out, not_3_out, not_4_out, not_5_out, or_2_out, xor_1_out,
       xor_2_out, xor_3_out;

  and and_1 (and_1_out, S[2], S[1]);
  or or_1 (Open, S[3], and_1_out);
  Multiplexer #(.Selector_Bits(2)) multiplexer_1 (
    .sel(Coin), .in_0(1'b0), .in_1(1'b0), .in_2(S[2]), .in_3(1'b1), .out(multiplexer_1_out));
  and and_2 (and_2_out, multiplexer_1_out, A);
  xor xor_1 (xor_1_out, S[1], S[2]);
  or or_2 (or_2_out, Open, reset);
  and and_3 (Change[0], S[0], Open);
  not not_1 (A, or_2_out);
  D_FF d_ff_1 (.D(and_2_out), .C(clock), .Q(S[3]));  // open: nQ
  not not_2 (not_2_out, S[2]);
  xor xor_2 (xor_2_out, S[1], S[0]);
  xor xor_3 (xor_3_out, S[1], S[2]);
  Multiplexer #(.Selector_Bits(2)) multiplexer_2 (
    .sel(Coin), .in_0(S[2]), .in_1(xor_1_out), .in_2(not_2_out), .in_3(xor_1_out), .out(multiplexer_2_out));
  D_FF d_ff_2 (.D(and_4_out), .C(clock), .Q(S[2]));  // open: nQ
  and and_4 (and_4_out, multiplexer_2_out, A);
  not not_3 (not_3_out, S[1]);
  not not_4 (not_4_out, S[1]);
  and and_5 (Change[3], S[1], S[2], S[3], Open);
  and and_6 (Change[1], S[3], ~S[1], Open);  // And
  and and_7 (Change[2], S[3], xor_3_out, Open);
  Multiplexer #(.Selector_Bits(2)) multiplexer_3 (
    .sel(Coin), .in_0(S[1]), .in_1(not_3_out), .in_2(xor_2_out), .in_3(not_4_out), .out(multiplexer_3_out));
  D_FF d_ff_3 (.D(and_8_out), .C(clock), .Q(S[1]));  // open: nQ
  and and_8 (and_8_out, multiplexer_3_out, A);
  not not_5 (not_5_out, S[0]);
  and and_9 (and_9_out, multiplexer_4_out, A);
  Multiplexer #(.Selector_Bits(2)) multiplexer_4 (
    .sel(Coin), .in_0(S[0]), .in_1(S[0]), .in_2(not_5_out), .in_3(S[0]), .out(multiplexer_4_out));
  D_FF d_ff_4 (.D(and_9_out), .C(clock), .Q(S[0]));  // open: nQ

  // Other names for the same wires on the sheet: C[1:0] = Coin; CH0 = Change[0]; CH1 = Change[1]; CH2 = Change[2];
  //   CH3 = Change[3]; CK = clock; O = Open; R = reset
endmodule

/* Test case T14:
reset Coin clock Open Change S
1 0 0 x x x
1 0 1 0 0 0
1 0 0 x x x
1 0 1 0 0 0
1 0 0 x x x
1 0 1 0 0 0
1 0 0 x x x
1 0 1 0 0 0
0 0 0 0 0 0
0 0 1 0 0 0
0 0 0 0 0 0
0 0 1 0 0 0
0 0 0 0 0 0
0 0 1 0 0 0
0 0 0 0 0 0
0 0 1 0 0 0
0 0 0 0 0 0
0 0 1 0 0 0
0 0 0 0 0 0
0 0 1 0 0 0
0 1 0 0 0 0
0 1 1 0 0 2
0 1 0 0 0 2
0 1 1 0 0 4
0 2 0 0 0 4
0 2 1 1 3 9
0 0 0 1 3 9
0 0 1 0 0 0
0 0 0 0 0 0
0 0 1 0 0 0
0 0 0 0 0 0
0 0 1 0 0 0
0 0 0 0 0 0
0 0 1 0 0 0
1 0 0 x x x
1 0 1 0 0 0
1 0 0 x x x
1 0 1 0 0 0
0 0 0 0 0 0
0 0 1 0 0 0
0 0 0 0 0 0
0 0 1 0 0 0
0 2 0 0 0 0
0 2 1 0 0 5
0 3 0 0 0 5
0 3 1 1 9 15
0 0 0 1 9 15
0 0 1 0 0 0
*/

/* Test case T12:
reset Coin clock Open Change S
1 0 0 x x x
1 0 1 0 0 0
0 1 0 0 0 0
0 1 1 0 0 2
1 0 0 x x x
1 0 1 0 0 0
0 0 0 0 0 0
0 0 1 0 0 0
0 1 0 0 0 0
0 1 1 0 0 2
0 1 0 0 0 2
0 1 1 0 0 4
1 0 0 x x x
1 0 1 0 0 0
0 0 0 0 0 0
0 0 1 0 0 0
0 2 0 0 0 0
0 2 1 0 0 5
1 0 0 x x x
1 0 1 0 0 0
0 0 0 0 0 0
0 0 1 0 0 0
0 1 0 0 0 0
0 1 1 0 0 2
0 1 0 0 0 2
0 1 1 0 0 4
0 1 0 0 0 4
0 1 1 1 0 6
0 0 0 1 0 6
0 0 1 0 0 0
0 2 0 0 0 0
0 2 1 0 0 5
0 0 0 0 0 5
0 0 1 0 0 5
1 0 0 x x x
1 0 1 0 0 0
0 3 0 0 0 0
0 3 1 1 4 10
0 0 0 1 4 10
0 0 1 0 0 0
*/

/* Test case T10:
reset Coin clock Open Change S
1 0 0 x x x
1 0 1 0 0 0
0 0 0 0 0 0
0 0 1 0 0 0
0 0 0 0 0 0
0 0 1 0 0 0
0 1 0 0 0 0
0 1 1 0 0 2
0 0 0 0 0 2
0 0 1 0 0 2
0 0 0 0 0 2
0 0 1 0 0 2
0 1 0 0 0 2
0 1 1 0 0 4
0 0 0 0 0 4
0 0 1 0 0 4
0 0 0 0 0 4
0 0 1 0 0 4
0 0 0 0 0 4
0 0 1 0 0 4
0 2 0 0 0 4
0 2 1 1 3 9
0 0 0 1 3 9
0 0 1 0 0 0
0 0 0 0 0 0
0 0 1 0 0 0
0 2 0 0 0 0
0 2 1 0 0 5
0 0 0 0 0 5
0 0 1 0 0 5
0 0 0 0 0 5
0 0 1 0 0 5
0 3 0 0 0 5
0 3 1 1 9 15
0 0 0 1 9 15
0 0 1 0 0 0
0 1 0 0 0 0
0 1 1 0 0 2
0 0 0 0 0 2
0 0 1 0 0 2
0 2 0 0 0 2
0 2 1 1 1 7
0 0 0 1 1 7
0 0 1 0 0 0
0 0 0 0 0 0
0 0 1 0 0 0
*/

/* Test case T09:
reset Coin clock Open Change S
1 0 0 x x x
1 0 1 0 0 0
0 1 0 0 0 0
0 1 1 0 0 2
0 1 0 0 0 2
0 1 1 0 0 4
0 3 0 0 0 4
0 3 1 1 8 14
0 0 0 1 8 14
0 0 1 0 0 0
0 0 0 0 0 0
0 0 1 0 0 0
*/

/* Test case T07:
reset Coin clock Open Change S
1 0 0 x x x
1 0 1 0 0 0
0 1 0 0 0 0
0 1 1 0 0 2
0 1 0 0 0 2
0 1 1 0 0 4
0 1 0 0 0 4
0 1 1 1 0 6
0 0 0 1 0 6
0 0 1 0 0 0
0 0 0 0 0 0
0 0 1 0 0 0
*/

/* Test case T05:
reset Coin clock Open Change S
1 0 0 x x x
1 0 1 0 0 0
0 1 0 0 0 0
0 1 1 0 0 2
0 2 0 0 0 2
0 2 1 1 1 7
0 0 0 1 1 7
0 0 1 0 0 0
0 0 0 0 0 0
0 0 1 0 0 0
*/

/* Test case T02:
reset Coin clock Open Change S
1 0 0 x x x
1 0 1 0 0 0
0 2 0 0 0 0
0 2 1 0 0 5
0 1 0 0 0 5
0 1 1 1 1 7
0 0 0 1 1 7
0 0 1 0 0 0
0 0 0 0 0 0
0 0 1 0 0 0
*/

/* Test case T01:
reset Coin clock Open Change S
1 0 0 x x x
1 0 1 0 0 0
0 3 0 0 0 0
0 3 1 1 4 10
0 0 0 1 4 10
0 0 1 0 0 0
0 0 0 0 0 0
0 0 1 0 0 0
*/
