// Digital circuit 7_01Template.dig as structural Verilog
module _7_01Template (
  input  [7:0] A,
  input  [7:0] B,
  input  start,
  input  reset,
  input  clock,
  output [7:0] gcd,
  output busy
);

  wire _00, _01, _10, _11, and_1_out, and_2_out, and_3_out, and_4_out, d_ff_1_q, Equal, Load_a, Load_b,
       Load_out, multiplexer_1_out, multiplexer_2_out, not_1_out, Qa, Qb, selector_a, selector_b, St;
  wire [7:0] multiplexer_3_out, multiplexer_4_out, multiplexer_5_out, multiplexer_6_out, multiplexer_7_out,
       multiplexer_8_out, multiplexer_9_out, sub_1_s, sub_2_s, Xn, Yn;

  Multiplexer #(.Selector_Bits(2)) multiplexer_1 (
    .sel({Qb, Qa}), .in_0(St), .in_1(1'b0), .in_2(Equal), .in_3(1'b0), .out(multiplexer_1_out));
  D_FF d_ff_1 (.D(start), .C(clock), .Q(d_ff_1_q));  // open: nQ
  and and_1 (and_1_out, ~reset, multiplexer_1_out);  // And
  D_FF d_ff_2 (.D(and_1_out), .C(clock), .Q(Qa));  // open: nQ
  and and_2 (and_2_out, ~d_ff_1_q, start);  // And
  Multiplexer #(.Selector_Bits(2)) multiplexer_2 (
    .sel({Qb, Qa}), .in_0(1'b0), .in_1(1'b1), .in_2(1'b1), .in_3(1'b0), .out(multiplexer_2_out));
  and and_3 (and_3_out, and_2_out, not_1_out);
  not not_1 (not_1_out, reset);
  Sub #(.Bits(8)) sub_1 (.a(Yn), .b(Xn), .c_i(1'b0), .s(sub_1_s));  // open: c_o
  and and_4 (and_4_out, ~reset, multiplexer_2_out);  // And
  D_FF d_ff_3 (.D(and_4_out), .C(clock), .Q(Qb));  // open: nQ
  Multiplexer #(.Bits(8)) multiplexer_3 (.sel(selector_b), .in_0(Yn), .in_1(sub_1_s), .out(multiplexer_3_out));
  D_FF d_ff_4 (.D(and_3_out), .C(clock), .Q(St));  // open: nQ
  Multiplexer #(.Bits(8)) multiplexer_4 (.sel(_01), .in_0(multiplexer_3_out), .in_1(B), .out(multiplexer_4_out));
  Multiplexer #(.Bits(8)) multiplexer_5 (
    .sel(reset), .in_0(multiplexer_4_out), .in_1({8{1'b0}}), .out(multiplexer_5_out));
  Decoder #(.Selector_Bits(2)) decoder_1 (.sel({Qb, Qa}), .out_0(_00), .out_1(_01), .out_2(_10), .out_3(_11));
  Register #(.Bits(8)) register_1 (.D(multiplexer_5_out), .C(clock), .en(Load_b), .Q(Yn));
  Comparator #(.Bits(8)) comparator_1 (.a(Xn), .b(Yn), .gt(selector_a), .eq(Equal), .lt(selector_b));
  or or_1 (busy, St, _01, _10);
  Sub #(.Bits(8)) sub_2 (.a(Xn), .b(Yn), .c_i(1'b0), .s(sub_2_s));  // open: c_o
  or or_2 (Load_out, _11, reset);
  or or_3 (Load_a, _01, reset, _10);
  or or_4 (Load_b, _01, reset, _10);
  Multiplexer #(.Bits(8)) multiplexer_6 (.sel(selector_a), .in_0(Xn), .in_1(sub_2_s), .out(multiplexer_6_out));
  Multiplexer #(.Bits(8)) multiplexer_7 (.sel(_01), .in_0(multiplexer_6_out), .in_1(A), .out(multiplexer_7_out));
  Multiplexer #(.Bits(8)) multiplexer_8 (.sel(reset), .in_0(Xn), .in_1({8{1'b0}}), .out(multiplexer_8_out));
  Multiplexer #(.Bits(8)) multiplexer_9 (
    .sel(reset), .in_0(multiplexer_7_out), .in_1({8{1'b0}}), .out(multiplexer_9_out));
  Register #(.Bits(8)) register_2 (.D(multiplexer_8_out), .C(clock), .en(Load_out), .Q(gcd));
  Register #(.Bits(8)) register_3 (.D(multiplexer_9_out), .C(clock), .en(Load_a), .Q(Xn));

  // Other names for the same wires on the sheet: CLK = clock; selector[1:0] = {Qb, Qa}; X[7:0] = A; Y[7:0] = B
endmodule

/* Test case T11:
A B start reset clock gcd busy
0 0 0 1 0 x x
0 0 0 1 1 0 0
255 1 1 0 0 x x
255 1 1 0 1 x 1
repeat(20) 255 1 0 0 C x x
255 1 0 1 0 x x
255 1 0 1 1 0 0
255 1 0 0 0 0 0
255 1 0 0 1 0 0
255 1 0 0 0 0 0
255 1 0 0 1 0 0
255 1 0 0 0 0 0
255 1 0 0 1 0 0
18 24 1 0 0 x x
18 24 1 0 1 x 1
repeat(600) 18 24 0 0 C x x
18 24 0 0 0 6 0
18 24 0 0 1 6 0
18 24 0 0 0 6 0
18 24 0 0 1 6 0
18 24 0 1 0 x x
18 24 0 1 1 0 0
18 24 0 1 0 x x
18 24 0 1 1 0 0
18 24 0 0 0 0 0
18 24 0 0 1 0 0
18 24 0 0 0 0 0
18 24 0 0 1 0 0
100 75 1 0 0 x x
100 75 1 0 1 x 1
repeat(600) 100 75 0 0 C x x
100 75 0 0 0 25 0
100 75 0 0 1 25 0
100 75 0 0 0 25 0
100 75 0 0 1 25 0
*/

/* Test case T09:
A B start reset clock gcd busy
0 0 0 1 0 x x
0 0 0 1 1 0 0
84 36 1 0 0 x x
84 36 1 0 1 x 1
repeat(600) 84 36 0 0 C x x
84 36 0 0 0 12 0
84 36 0 0 1 12 0
10 3 0 0 0 12 0
10 3 0 0 1 12 0
10 3 0 0 0 12 0
10 3 0 0 1 12 0
10 3 0 0 0 12 0
10 3 0 0 1 12 0
10 3 0 0 0 12 0
10 3 0 0 1 12 0
10 3 0 0 0 12 0
10 3 0 0 1 12 0
10 3 0 0 0 12 0
10 3 0 0 1 12 0
45 60 1 0 0 x x
45 60 1 0 1 x 1
repeat(600) 45 60 0 0 C x x
45 60 0 0 0 15 0
45 60 0 0 1 15 0
99 1 0 0 0 15 0
99 1 0 0 1 15 0
99 1 0 0 0 15 0
99 1 0 0 1 15 0
99 1 0 0 0 15 0
99 1 0 0 1 15 0
99 1 0 0 0 15 0
99 1 0 0 1 15 0
99 1 0 0 0 15 0
99 1 0 0 1 15 0
99 1 0 0 0 15 0
99 1 0 0 1 15 0
121 11 1 0 0 x x
121 11 1 0 1 x 1
repeat(600) 121 11 0 0 C x x
121 11 0 0 0 11 0
121 11 0 0 1 11 0
7 7 0 0 0 11 0
7 7 0 0 1 11 0
7 7 0 0 0 11 0
7 7 0 0 1 11 0
7 7 0 0 0 11 0
7 7 0 0 1 11 0
7 7 0 0 0 11 0
7 7 0 0 1 11 0
7 7 0 0 0 11 0
7 7 0 0 1 11 0
7 7 0 0 0 11 0
7 7 0 0 1 11 0
*/

/* Test case T07:
A B start reset clock gcd busy
0 0 0 1 0 x x
0 0 0 1 1 0 0
255 1 1 0 0 x x
255 1 1 0 1 x 1
repeat(600) 255 1 0 0 C x x
255 1 0 0 0 1 0
255 1 0 0 1 1 0
255 1 0 0 0 1 0
255 1 0 0 1 1 0
1 255 1 0 0 x x
1 255 1 0 1 x 1
repeat(600) 1 255 0 0 C x x
1 255 0 0 0 1 0
1 255 0 0 1 1 0
1 255 0 0 0 1 0
1 255 0 0 1 1 0
255 254 1 0 0 x x
255 254 1 0 1 x 1
repeat(600) 255 254 0 0 C x x
255 254 0 0 0 1 0
255 254 0 0 1 1 0
255 254 0 0 0 1 0
255 254 0 0 1 1 0
254 255 1 0 0 x x
254 255 1 0 1 x 1
repeat(600) 254 255 0 0 C x x
254 255 0 0 0 1 0
254 255 0 0 1 1 0
254 255 0 0 0 1 0
254 255 0 0 1 1 0
*/

/* Test case T06:
A B start reset clock gcd busy
0 0 0 1 0 x x
0 0 0 1 1 0 0
1 200 1 0 0 x x
1 200 1 0 1 x 1
repeat(600) 1 200 0 0 C x x
1 200 0 0 0 1 0
1 200 0 0 1 1 0
1 200 0 0 0 1 0
1 200 0 0 1 1 0
200 1 1 0 0 x x
200 1 1 0 1 x 1
repeat(600) 200 1 0 0 C x x
200 1 0 0 0 1 0
200 1 0 0 1 1 0
200 1 0 0 0 1 0
200 1 0 0 1 1 0
2 1 1 0 0 x x
2 1 1 0 1 x 1
repeat(600) 2 1 0 0 C x x
2 1 0 0 0 1 0
2 1 0 0 1 1 0
2 1 0 0 0 1 0
2 1 0 0 1 1 0
*/

/* Test case T05:
A B start reset clock gcd busy
0 0 0 1 0 x x
0 0 0 1 1 0 0
84 36 1 0 0 x x
84 36 1 0 1 x 1
repeat(600) 84 36 0 0 C x x
84 36 0 0 0 12 0
84 36 0 0 1 12 0
84 36 0 0 0 12 0
84 36 0 0 1 12 0
36 84 1 0 0 x x
36 84 1 0 1 x 1
repeat(600) 36 84 0 0 C x x
36 84 0 0 0 12 0
36 84 0 0 1 12 0
36 84 0 0 0 12 0
36 84 0 0 1 12 0
120 75 1 0 0 x x
120 75 1 0 1 x 1
repeat(600) 120 75 0 0 C x x
120 75 0 0 0 15 0
120 75 0 0 1 15 0
120 75 0 0 0 15 0
120 75 0 0 1 15 0
*/

/* Test case T02:
A B start reset clock gcd busy
0 0 0 1 0 x x
0 0 0 1 1 0 0
48 12 1 0 0 x x
48 12 1 0 1 x 1
repeat(600) 48 12 0 0 C x x
48 12 0 0 0 12 0
48 12 0 0 1 12 0
48 12 0 0 0 12 0
48 12 0 0 1 12 0
255 5 1 0 0 x x
255 5 1 0 1 x 1
repeat(600) 255 5 0 0 C x x
255 5 0 0 0 5 0
255 5 0 0 1 5 0
255 5 0 0 0 5 0
255 5 0 0 1 5 0
128 2 1 0 0 x x
128 2 1 0 1 x 1
repeat(600) 128 2 0 0 C x x
128 2 0 0 0 2 0
128 2 0 0 1 2 0
128 2 0 0 0 2 0
128 2 0 0 1 2 0
*/

/* Test case T01:
A B start reset clock gcd busy
0 0 0 1 0 x x
0 0 0 1 1 0 0
12 12 1 0 0 x x
12 12 1 0 1 x 1
repeat(600) 12 12 0 0 C x x
12 12 0 0 0 12 0
12 12 0 0 1 12 0
12 12 0 0 0 12 0
12 12 0 0 1 12 0
200 200 1 0 0 x x
200 200 1 0 1 x 1
repeat(600) 200 200 0 0 C x x
200 200 0 0 0 200 0
200 200 0 0 1 200 0
200 200 0 0 0 200 0
200 200 0 0 1 200 0
1 1 1 0 0 x x
1 1 1 0 1 x 1
repeat(600) 1 1 0 0 C x x
1 1 0 0 0 1 0
1 1 0 0 1 1 0
1 1 0 0 0 1 0
1 1 0 0 1 1 0
*/
