// Digital circuit 2.dig as structural Verilog
module _2 (
  input  X3,
  input  X2,
  input  X1,
  input  X0,
  output Q2,
  output Q1,
  output Q0,
  output R1,
  output R0
);

  wire and_1_out, and_2_out, and_3_out, and_4_out, and_5_out, and_6_out, and_7_out, and_8_out, and_9_out,
       and_10_out, and_11_out, and_12_out, and_13_out, and_14_out, and_15_out, and_16_out, and_17_out,
       not_1_out, not_2_out, not_3_out, not_4_out;

  not not_1 (not_1_out, X3);
  not not_2 (not_2_out, X2);
  not not_3 (not_3_out, X1);
  not not_4 (not_4_out, X0);
  and and_1 (and_1_out, X1, X2, not_1_out);
  and and_2 (and_2_out, not_2_out, X3);
  and and_3 (and_3_out, X0, X1, not_2_out);
  and and_4 (and_4_out, X0, X1, X3);
  and and_5 (and_5_out, not_3_out, X2, not_1_out);
  and and_6 (and_6_out, X0, not_2_out, X3);
  and and_7 (and_7_out, X1, not_2_out, X3);
  and and_8 (and_8_out, not_4_out, X1, not_2_out, not_1_out);
  and and_9 (and_9_out, X0, not_3_out, X2, not_1_out);
  and and_10 (and_10_out, not_4_out, X1, X2, X3);
  and and_11 (and_11_out, X0, X1, not_2_out, X3);
  and and_12 (and_12_out, not_4_out, not_3_out, not_2_out, X3);
  and and_13 (and_13_out, X0, not_3_out, not_2_out, not_1_out);
  and and_14 (and_14_out, not_4_out, not_3_out, X2, not_1_out);
  and and_15 (and_15_out, X0, X1, X2, not_1_out);
  and and_16 (and_16_out, X0, not_3_out, X2, X3);
  and and_17 (and_17_out, not_4_out, X1, not_2_out, X3);
  and and_18 (Q2, X2, X3);
  or or_1 (Q1, and_1_out, and_2_out);
  or or_2 (Q0, and_3_out, and_4_out, and_5_out, and_6_out, and_7_out);
  or or_3 (R1, and_8_out, and_9_out, and_10_out, and_11_out, and_12_out);
  or or_4 (R0, and_13_out, and_14_out, and_15_out, and_16_out, and_17_out);

  // Notes on the sheet:
  //   Q2: Quotient bit 2
  //   Q1: Quotient bit 1
  //   Q0: Quotient bit 0
  //   R1: Remainder bit 1
  //   R0: Remainder bit 0
  //   Don't change anything inside this box
endmodule

/* Test case test:
X3 X2 X1 X0 Q2 Q1 Q0 R1 R0
0 0 0 0 0 0 0 0 0
0 0 0 1 0 0 0 0 1
0 0 1 0 0 0 0 1 0
0 0 1 1 0 0 1 0 0
0 1 0 0 0 0 1 0 1
0 1 0 1 0 0 1 1 0
0 1 1 0 0 1 0 0 0
0 1 1 1 0 1 0 0 1
1 0 0 0 0 1 0 1 0
1 0 0 1 0 1 1 0 0
1 0 1 0 0 1 1 0 1
1 0 1 1 0 1 1 1 0
1 1 0 0 1 0 0 0 0
1 1 0 1 1 0 0 0 1
1 1 1 0 1 0 0 1 0
1 1 1 1 1 0 1 0 0
*/

/* Test case T1:
X3 X2 X1 X0 Q2 Q1 Q0 R1 R0
0 0 0 0 0 0 0 0 0
0 1 1 1 0 1 0 0 1
1 1 1 1 1 0 1 0 0
*/
