// Digital circuit Exam2_1_Template.dig as structural Verilog
module Exam2_1_Template (
  input  reset,
  input  X,
  input  Y,
  input  Z,
  input  load,
  input  clock,
  output A,
  output B,
  output C
);

  wire and_1_out, and_2_out, and_3_out, and_4_out, and_5_out, and_6_out, and_7_out, and_8_out, and_9_out,
       and_10_out, and_12_out, and_13_out, and_14_out, d_ff_1_q, d_ff_2_q, d_ff_3_q, multiplexer_1_out,
       multiplexer_2_out, multiplexer_3_out, or_1_out, or_3_out, or_5_out, or_6_out, or_7_out, or_8_out, re;

  and and_1 (and_1_out, load, X);
  and and_2 (and_2_out, A, ~B, C, ~clock, ~reset);  // And
  Multiplexer multiplexer_1 (.sel(re), .in_0(or_1_out), .in_1(1'b1), .out(multiplexer_1_out));
  or or_1 (or_1_out, and_1_out, and_4_out);
  and and_3 (and_3_out, ~A, ~B);  // And
  or or_2 (re, and_2_out, reset);
  D_FF d_ff_1 (.D(multiplexer_1_out), .C(clock), .Q(d_ff_1_q));  // open: nQ
  and and_4 (and_4_out, ~load, or_3_out);  // And
  or or_3 (or_3_out, and_3_out, and_5_out);
  and and_5 (and_5_out, ~B, ~C);  // And
  or or_4 (A, d_ff_1_q, reset);
  and and_6 (and_6_out, ~A, ~B, C);  // And
  and and_7 (and_7_out, ~load, or_5_out);  // And
  or or_5 (or_5_out, and_6_out, and_8_out, and_9_out);
  and and_8 (and_8_out, A, B);
  Multiplexer multiplexer_2 (.sel(re), .in_0(or_6_out), .in_1(1'b0), .out(multiplexer_2_out));
  and and_9 (and_9_out, B, ~C);  // And
  or or_6 (or_6_out, and_7_out, and_10_out);
  D_FF d_ff_2 (.D(multiplexer_2_out), .C(clock), .Q(d_ff_2_q));  // open: nQ
  and and_10 (and_10_out, load, Y);
  and and_11 (B, ~reset, d_ff_2_q);  // And
  and and_12 (and_12_out, ~load, or_8_out);  // And
  Multiplexer multiplexer_3 (.sel(re), .in_0(or_7_out), .in_1(1'b1), .out(multiplexer_3_out));
  or or_7 (or_7_out, and_12_out, and_14_out);
  or or_8 (or_8_out, A, and_13_out);
  and and_13 (and_13_out, B, ~C);  // And
  D_FF d_ff_3 (.D(multiplexer_3_out), .C(clock), .Q(d_ff_3_q));  // open: nQ
  or or_9 (C, d_ff_3_q, reset);
  and and_14 (and_14_out, load, Z);

  // Other names for the same wires on the sheet: CLK = clock
endmodule

/* Test case T01:
X Y Z reset load clock A B C
0 0 0 1     0    0     x x x
0 0 0 1     0    1     1 0 1
0 0 0 0     0    0     1 0 1
0 0 0 0     0    1     0 0 1
0 0 0 0     0    0     0 0 1
0 0 0 0     0    1     1 1 0
0 0 0 0     0    0     1 1 0
0 0 0 0     0    1     0 1 1
0 0 0 0     0    0     0 1 1
0 0 0 0     0    1     0 0 0
0 0 0 0     0    0     0 0 0
1 1 0 0     1    0     0 0 0
1 1 0 0     1    1     1 1 0
1 1 0 0     1    0     1 1 0
0 0 0 0     0    0     1 1 0
0 0 0 0     0    1     0 1 1
0 0 0 0     0    0     0 1 1
0 0 0 0     0    1     0 0 0
0 0 0 0     0    0     0 0 0
0 0 0 0     0    1     1 0 0
0 0 0 0     0    0     1 0 0
0 0 0 1     0    0     1 0 1
0 0 0 0     0    0     1 0 1
0 0 0 0     0    1     0 0 1
0 0 0 0     0    0     0 0 1
0 0 0 0     0    1     1 1 0
0 0 0 0     0    0     1 1 0
0 0 0 0     0    1     0 1 1
0 0 0 0     0    0     0 1 1
0 0 0 0     0    1     0 0 0
0 0 0 1     0    1     1 0 1
0 0 0 0     0    1     1 0 1
0 0 0 0     0    0     1 0 1
0 0 0 0     0    1     0 0 1
0 0 0 0     0    0     0 0 1
0 0 0 0     0    1     1 1 0
0 0 0 0     0    0     1 1 0
0 0 0 0     0    1     0 1 1
0 0 0 0     0    0     0 1 1
0 0 0 0     0    1     0 0 0
0 0 0 0     0    0     0 0 0
0 0 0 0     0    1     1 0 0
0 0 0 0     0    0     1 0 0
0 0 0 0     0    1     1 0 1
0 0 0 0     0    0     1 0 1
*/
