// Digital circuit Exam2_2_Template.dig as structural Verilog
module Exam2_2_Template (
  input  [15:0] A,
  input  [15:0] D,
  input  [15:0] N,
  input  start,
  input  reset,
  input  clock,
  output [15:0] K,
  output [15:0] S,
  output busy
);

  wire _00, _01, _10, _11, and_1_out, and_2_out, and_4_out, comparator_1_lt, comparator_2_eq, d_ff_2_q,
       loadA, loadK, loadout, loadS, multiplexer_1_out, multiplexer_4_out, Q_a, Q_b, st;
  wire [15:0] add_1_s, add_2_s, add_3_s, An, K_t, multiplexer_2_out, multiplexer_3_out, multiplexer_5_out,
       multiplexer_6_out, multiplexer_7_out, S_t;

  Comparator #(.Bits(16)) comparator_1 (.a(S_t), .b(N), .lt(comparator_1_lt));  // open: gt, eq
  Add #(.Bits(16)) add_1 (.a(An), .b(D), .c_i(1'b0), .s(add_1_s));  // open: c_o
  Multiplexer #(.Selector_Bits(2)) multiplexer_1 (
    .sel({Q_a, Q_b}), .in_0(1'b0), .in_1(comparator_1_lt), .in_2(1'b1), .in_3(1'b0), .out(multiplexer_1_out));
  Add #(.Bits(16)) add_2 (.a(An), .b(S_t), .c_i(1'b0), .s(add_2_s));  // open: c_o
  and and_1 (and_1_out, multiplexer_1_out, ~reset);  // And
  Comparator #(.Bits(16)) comparator_2 (.a(K_t), .b({16{1'b0}}), .eq(comparator_2_eq));  // open: gt, lt
  D_FF d_ff_1 (.D(and_1_out), .C(clock), .Q(Q_a));  // open: nQ
  D_FF d_ff_2 (.D(start), .C(clock), .Q(d_ff_2_q));  // open: nQ
  Multiplexer #(.Bits(16)) multiplexer_2 (.sel(reset), .in_0(add_2_s), .in_1({16{1'b0}}), .out(multiplexer_2_out));
  Multiplexer #(.Bits(16)) multiplexer_3 (.sel(_00), .in_0(add_1_s), .in_1(A), .out(multiplexer_3_out));
  and and_2 (and_2_out, comparator_2_eq, st);
  and and_3 (st, ~d_ff_2_q, start);  // And
  Register #(.Bits(16)) register_1 (.D(multiplexer_2_out), .C(clock), .en(loadS), .Q(S_t));
  Register #(.Bits(16)) register_2 (.D(multiplexer_3_out), .C(clock), .en(loadA), .Q(An));
  Multiplexer #(.Selector_Bits(2)) multiplexer_4 (
    .sel({Q_a, Q_b}), .in_0(and_2_out), .in_1(1'b0), .in_2(1'b1), .in_3(1'b1), .out(multiplexer_4_out));
  and and_4 (and_4_out, multiplexer_4_out, ~reset);  // And
  Multiplexer #(.Bits(16)) multiplexer_5 (.sel(reset), .in_0(K_t), .in_1({16{1'b0}}), .out(multiplexer_5_out));
  Multiplexer #(.Bits(16)) multiplexer_6 (.sel(reset), .in_0(S_t), .in_1({16{1'b0}}), .out(multiplexer_6_out));
  Decoder #(.Selector_Bits(2)) decoder_1 (.sel({Q_a, Q_b}), .out_0(_00), .out_1(_01), .out_2(_10), .out_3(_11));
  Add #(.Bits(16)) add_3 (.a(K_t), .b(16'h1), .c_i(1'b0), .s(add_3_s));  // open: c_o
  D_FF d_ff_3 (.D(and_4_out), .C(clock), .Q(Q_b));  // open: nQ
  Register #(.Bits(16)) register_3 (.D(multiplexer_5_out), .C(clock), .en(loadout), .Q(K));
  Register #(.Bits(16)) register_4 (.D(multiplexer_6_out), .C(clock), .en(loadout), .Q(S));
  Multiplexer #(.Bits(16)) multiplexer_7 (.sel(reset), .in_0(add_3_s), .in_1({16{1'b0}}), .out(multiplexer_7_out));
  or or_1 (loadA, _00, _11);
  or or_2 (loadout, _00, reset);
  Register #(.Bits(16)) register_5 (.D(multiplexer_7_out), .C(clock), .en(loadK), .Q(K_t));
  not not_1 (busy, _00);
  or or_3 (loadS, _10, reset);
  or or_4 (loadK, _11, reset);

  // Other names for the same wires on the sheet: CLK = clock; state[1:0] = {Q_a, Q_b}
endmodule

/* Test case T01:
A D N start reset clock K S busy
0  0  0   0     1     0     x x x
0  0  0   0     1     1     0 0 0
0  0  0   0     0     0     0 0 0
3  2  20  1     0     0     0 0 0
3  2  20  1     0     1     x x 1
3  2  20  0     0     0     x x x
3  2  20  0     0     1     x x x
3  2  20  0     0     0     x x x
3  2  20  0     0     1     x x x
3  2  20  0     0     0     x x x
3  2  20  0     0     1     x x x
3  2  20  0     0     0     x x x
3  2  20  0     0     1     x x x
3  2  20  0     0     0     x x x
3  2  20  0     0     1     x x x
3  2  20  0     0     0     x x x
3  2  20  0     0     1     x x x
3  2  20  0     0     0     x x x
3  2  20  0     0     1     x x x
3  2  20  0     0     0     x x x
3  2  20  0     0     1     x x x
3  2  20  0     0     0     x x x
3  2  20  0     0     1     x x x
3  2  20  0     0     0     x x x
3  2  20  0     0     1     x x x
3  2  20  0     0     0     x x x
3  2  20  0     0     1     x x x
3  2  20  0     0     0     x x x
3  2  20  0     0     1     x x x
3  2  20  0     0     0     x x x
3  2  20  0     0     1     x x x
3  2  20  0     0     0     x x x
3  2  20  0     0     1     x x x
3  2  20  0     0     0     x x x
3  2  20  0     0     1     x x x
3  2  20  0     0     0     x x x
3  2  20  0     0     1     x x x
3  2  20  0     0     0     x x x
3  2  20  0     0     1     x x x
3  2  20  0     0     0     x x x
3  2  20  0     0     1     x x x
3  2  20  0     0     0     x x x
3  2  20  0     0     1     x x x
3  2  20  0     0     0     x x x
3  2  20  0     0     1     x x x
3  2  20  0     0     0     x x x
3  2  20  0     0     1     x x x
3  2  20  0     0     0     x x x
3  2  20  0     0     1     4 24 0
3  2  20  0     0     0     4 24 0
3  2  20  0     0     1     4 24 0
3  2  20  0     0     0     4 24 0
4  3  97  0     0     0     4 24 0
4  3  97  0     0     1     4 24 0
4  3  97  0     0     0     4 24 0
4  3  97  1     0     0     4 24 0
4  3  97  1     0     1     4 24 0
4  3  97  0     0     0     4 24 0
4  3  97  0     0     1     4 24 0
4  3  97  0     0     0     4 24 0
4  3  97  0     0     1     4 24 0
4  3  97  0     0     0     4 24 0
4  3  97  0     0     1     4 24 0
4  3  97  0     0     0     4 24 0
4  3  97  0     1     0     x x x
4  3  97  0     1     1     0 0 0
4  3  97  0     0     0     0 0 0
5  3  60  1     0     0     0 0 0
5  3  60  1     0     1     x x 1
5  3  60  0     0     0     x x x
5  3  60  0     0     1     x x x
5  3  60  0     0     0     x x x
5  3  60  0     0     1     x x x
5  3  60  0     0     0     x x x
5  3  60  0     0     1     x x x
5  3  60  0     0     0     x x x
5  3  60  0     1     0     x x x
5  3  60  0     1     1     0 0 0
5  3  60  0     0     0     0 0 0
5  3  60  0     0     1     0 0 0
5  3  60  0     0     0     0 0 0
5  3  60  0     0     1     0 0 0
5  3  60  0     0     0     0 0 0
1  1  10  1     0     0     0 0 0
1  1  10  1     0     1     x x 1
1  1  10  0     0     0     x x x
1  1  10  0     0     1     x x x
1  1  10  0     0     0     x x x
1  1  10  0     0     1     x x x
1  1  10  0     0     0     x x x
1  1  10  0     0     1     x x x
1  1  10  0     0     0     x x x
1  1  10  0     0     1     x x x
1  1  10  0     0     0     x x x
1  1  10  0     0     1     x x x
1  1  10  0     0     0     x x x
1  1  10  0     0     1     x x x
1  1  10  0     0     0     x x x
1  1  10  0     0     1     x x x
1  1  10  0     0     0     x x x
1  1  10  0     0     1     x x x
1  1  10  0     0     0     x x x
1  1  10  0     0     1     x x x
1  1  10  0     0     0     x x x
1  1  10  0     0     1     x x x
1  1  10  0     0     0     x x x
1  1  10  0     0     1     x x x
1  1  10  0     0     0     x x x
1  1  10  0     0     1     x x x
1  1  10  0     0     0     x x x
1  1  10  0     0     1     x x x
1  1  10  0     0     0     x x x
1  1  10  0     0     1     x x x
1  1  10  0     0     0     x x x
1  1  10  0     0     1     x x x
1  1  10  0     0     0     x x x
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*/
