// Digital circuit Exam2_3_Template.dig as structural Verilog
module Exam2_3_Template (
  input  [7:0] N,
  input  \new ,
  input  reset,
  input  clock,
  output [7:0] ones,
  output [7:0] odd,
  output busy
);

  wire _00, _01, _10, _11, and_1_out, and_3_out, d_ff_2_q, load_odd, load_ones, multiplexer_1_out,
       multiplexer_3_out, Q_a, Q_b, st;
  wire [3:0] bitcount_1_out, bitcount_2_out;
  wire [7:0] add_1_s, add_2_s, multiplexer_2_out, multiplexer_4_out, N_n;

  BitCount #(.Bits(8)) bitcount_1 (.in(N_n), .out(bitcount_1_out));
  BitCount #(.Bits(8)) bitcount_2 (.in(N_n), .out(bitcount_2_out));
  Multiplexer #(.Selector_Bits(2)) multiplexer_1 (
    .sel({Q_a, Q_b}), .in_0(1'b0), .in_1(bitcount_1_out[0]), .in_2(1'b0), .in_3(1'b0), .out(multiplexer_1_out));
  Add #(.Bits(8)) add_1 (.a({4'b0000, bitcount_2_out}), .b(ones), .c_i(1'b0), .s(add_1_s));  // open: c_o
  and and_1 (and_1_out, multiplexer_1_out, ~reset);  // And
  D_FF d_ff_1 (.D(and_1_out), .C(clock), .Q(Q_a));  // open: nQ
  Multiplexer #(.Bits(8)) multiplexer_2 (.sel(reset), .in_0(add_1_s), .in_1({8{1'b0}}), .out(multiplexer_2_out));
  D_FF d_ff_2 (.D(\new ), .C(clock), .Q(d_ff_2_q));  // open: nQ
  Register #(.Bits(8)) register_1 (.D(N), .C(clock), .en(_00), .Q(N_n));
  Multiplexer #(.Selector_Bits(2)) multiplexer_3 (
    .sel({Q_a, Q_b}), .in_0(st), .in_1(1'b0), .in_2(1'b0), .in_3(1'b0), .out(multiplexer_3_out));
  and and_2 (st, \new , ~d_ff_2_q);  // And
  Register #(.Bits(8)) register_2 (.D(multiplexer_2_out), .C(clock), .en(load_ones), .Q(ones));
  and and_3 (and_3_out, multiplexer_3_out, ~reset);  // And
  D_FF d_ff_3 (.D(and_3_out), .C(clock), .Q(Q_b));  // open: nQ
  Decoder #(.Selector_Bits(2)) decoder_1 (.sel({Q_a, Q_b}), .out_0(_00), .out_1(_01), .out_2(_10), .out_3(_11));
  not not_1 (busy, _00);
  or or_1 (load_ones, _01, reset);
  Add #(.Bits(8)) add_2 (.a(8'h1), .b(odd), .c_i(1'b0), .s(add_2_s));  // open: c_o
  Multiplexer #(.Bits(8)) multiplexer_4 (.sel(reset), .in_0(add_2_s), .in_1({8{1'b0}}), .out(multiplexer_4_out));
  or or_2 (load_odd, _10, reset);
  Register #(.Bits(8)) register_3 (.D(multiplexer_4_out), .C(clock), .en(load_odd), .Q(odd));

  // Other names for the same wires on the sheet: CLK = clock; load_n = _00; State[1:0] = {Q_a, Q_b}
endmodule

/* Test case T01:
N new reset clock ones odd busy
0   0   1     0     x x x
0   0   1     1     0 0 0
0   0   0     0     0 0 0
5   1   0     0     0 0 0
5   1   0     1     x x 1
5   0   0     0     x x x
5   0   0     1     x x x
5   0   0     0     x x x
5   0   0     1     x x x
5   0   0     0     x x x
5   0   0     1     x x x
5   0   0     0     x x x
5   0   0     1     x x x
5   0   0     0     x x x
5   0   0     1     x x x
5   0   0     0     x x x
5   0   0     1     x x x
5   0   0     0     x x x
5   0   0     1     x x x
5   0   0     0     x x x
5   0   0     1     x x x
5   0   0     0     x x x
5   0   0     1     x x x
5   0   0     0     x x x
5   0   0     1     x x x
5   0   0     0     x x x
5   0   0     1     x x x
5   0   0     0     x x x
5   0   0     1     x x x
5   0   0     0     x x x
5   0   0     1     x x x
5   0   0     0     x x x
5   0   0     1     x x x
5   0   0     0     x x x
5   0   0     1     2 0 0
5   0   0     0     2 0 0
5   0   0     1     2 0 0
5   0   0     0     2 0 0
7   1   0     0     2 0 0
7   1   0     1     x x 1
7   0   0     0     x x x
7   0   0     1     x x x
7   0   0     0     x x x
7   0   0     1     x x x
7   0   0     0     x x x
7   0   0     1     x x x
7   0   0     0     x x x
7   0   0     1     x x x
7   0   0     0     x x x
7   0   0     1     x x x
7   0   0     0     x x x
7   0   0     1     x x x
7   0   0     0     x x x
7   0   0     1     x x x
7   0   0     0     x x x
7   0   0     1     x x x
7   0   0     0     x x x
7   0   0     1     x x x
7   0   0     0     x x x
7   0   0     1     x x x
7   0   0     0     x x x
7   0   0     1     x x x
7   0   0     0     x x x
7   0   0     1     x x x
7   0   0     0     x x x
7   0   0     1     x x x
7   0   0     0     x x x
7   0   0     1     x x x
7   0   0     0     x x x
7   0   0     1     5 1 0
7   0   0     0     5 1 0
7   0   0     1     5 1 0
7   0   0     0     5 1 0
255 1   0     0     5 1 0
255 1   0     1     x x 1
255 0   0     0     x x x
255 0   0     1     x x x
255 0   0     0     x x x
255 0   0     1     x x x
255 0   0     0     x x x
255 0   0     1     x x x
255 0   0     0     x x x
255 0   0     1     x x x
255 0   0     0     x x x
255 0   0     1     x x x
255 0   0     0     x x x
255 0   0     1     x x x
255 0   0     0     x x x
255 0   0     1     x x x
255 0   0     0     x x x
255 0   0     1     x x x
255 0   0     0     x x x
255 0   0     1     x x x
255 0   0     0     x x x
255 0   0     1     x x x
255 0   0     0     x x x
255 0   0     1     x x x
255 0   0     0     x x x
255 0   0     1     x x x
255 0   0     0     x x x
255 0   0     1     x x x
255 0   0     0     x x x
255 0   0     1     x x x
255 0   0     0     x x x
255 0   0     1     13 1 0
255 0   0     0     13 1 0
255 0   0     1     13 1 0
255 0   0     0     13 1 0
0   1   0     0     13 1 0
0   1   0     1     x x 1
0   0   0     0     x x x
0   0   0     1     x x x
0   0   0     0     x x x
0   0   0     1     x x x
0   0   0     0     x x x
0   0   0     1     x x x
0   0   0     0     x x x
0   0   0     1     x x x
0   0   0     0     x x x
0   0   0     1     x x x
0   0   0     0     x x x
0   0   0     1     x x x
0   0   0     0     x x x
0   0   0     1     x x x
0   0   0     0     x x x
0   0   0     1     x x x
0   0   0     0     x x x
0   0   0     1     x x x
0   0   0     0     x x x
0   0   0     1     x x x
0   0   0     0     x x x
0   0   0     1     x x x
0   0   0     0     x x x
0   0   0     1     x x x
0   0   0     0     x x x
0   0   0     1     x x x
0   0   0     0     x x x
0   0   0     1     x x x
0   0   0     0     x x x
0   0   0     1     13 1 0
0   0   0     0     13 1 0
0   0   0     1     13 1 0
0   0   0     0     13 1 0
128 1   0     0     13 1 0
128 1   0     1     x x 1
128 0   0     0     x x x
128 0   0     1     x x x
128 0   0     0     x x x
128 0   0     1     x x x
128 0   0     0     x x x
128 0   0     1     x x x
128 0   0     0     x x x
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*/
